// Digital circuit alu.dig as structural Verilog
module alu (
  input  [4:0] opcode,
  input  [15:0] X,
  input  [15:0] Y,
  output [15:0] Z,
  output [15:0] remainder,
  output overflow
);

  wire add_1_c_o, compare_1_p4, sub_1_c_o;
  wire [15:0] add_1_s, and_1_out, barrelshifter_1_out, barrelshifter_2_out, div_1_q, multiplexer_1_out,
       multiplexer_2_out, multiplexer_3_out, multiplexer_4_out, multiplexer_5_out, multiplexer_6_out,
       multiplexer_7_out, multiplexer_8_out, multiplexer_9_out, multiplexer_10_out, multiplexer_11_out,
       multiplexer_12_out, multiplexer_13_out, multiplexer_14_out, nand_1_out, nor_1_out, not_1_out,
       not_2_out, or_1_out, sub_1_s, xnor_1_out, xor_1_out;
  wire [31:0] mul_1_mul;

  Add #(.Bits(16)) add_1 (.a(X), .b(Y), .c_i(1'b0), .s(add_1_s), .c_o(add_1_c_o));
  Sub #(.Bits(16)) sub_1 (.a(X), .b(Y), .c_i(1'b0), .s(sub_1_s), .c_o(sub_1_c_o));
  Mul #(.Signed("true"), .Bits(16)) mul_1 (.a(X), .b(Y), .mul(mul_1_mul));
  Div #(.Signed("true"), .Bits(16)) div_1 (.a(X), .b(Y), .q(div_1_q), .r(remainder));
  BarrelShifter #(.Bits(16), .barrelSigned("true"), .direction("right")) barrelshifter_1 (
    .in(X), .shift(Y[5:0]), .out(barrelshifter_1_out));
  BarrelShifter #(.Bits(16), .barrelSigned("true")) barrelshifter_2 (.in(X), .shift(Y[5:0]), .out(barrelshifter_2_out));
  assign and_1_out = X & Y;  // And and_1, 16 bits wide
  assign or_1_out = X | Y;  // Or or_1, 16 bits wide
  assign not_1_out = ~X;  // Not not_1, 16 bits wide
  assign not_2_out = ~Y;  // Not not_2, 16 bits wide
  assign xor_1_out = X ^ Y;  // XOr xor_1, 16 bits wide
  assign xnor_1_out = ~(X ^ Y);  // XNOr xnor_1, 16 bits wide
  assign nor_1_out = ~(X | Y);  // NOr nor_1, 16 bits wide
  assign nand_1_out = ~(X & Y);  // NAnd nand_1, 16 bits wide
  // compare compare_1: pin names not known; wires that end beside it: opcode[2:0], X, Y, compare_1_p4
  or or_2 (overflow, add_1_c_o, sub_1_c_o);
  Multiplexer #(.Bits(16)) multiplexer_1 (.sel(opcode[0]), .in_0(add_1_s), .in_1(sub_1_s), .out(multiplexer_1_out));
  Multiplexer #(.Bits(16)) multiplexer_2 (
    .sel(opcode[0]), .in_0(mul_1_mul[15:0]), .in_1(div_1_q), .out(multiplexer_2_out));
  Multiplexer #(.Bits(16)) multiplexer_3 (
    .sel(opcode[0]), .in_0(barrelshifter_1_out), .in_1(barrelshifter_2_out), .out(multiplexer_3_out));
  Multiplexer #(.Bits(16)) multiplexer_4 (.sel(opcode[0]), .in_0(and_1_out), .in_1(or_1_out), .out(multiplexer_4_out));
  Multiplexer #(.Bits(16)) multiplexer_5 (.sel(opcode[0]), .in_0(not_1_out), .in_1(not_2_out), .out(multiplexer_5_out));
  Multiplexer #(.Bits(16)) multiplexer_6 (
    .sel(opcode[0]), .in_0(xor_1_out), .in_1(xnor_1_out), .out(multiplexer_6_out));
  Multiplexer #(.Bits(16)) multiplexer_7 (
    .sel(opcode[0]), .in_0(nor_1_out), .in_1(nand_1_out), .out(multiplexer_7_out));
  Multiplexer #(.Bits(16)) multiplexer_8 (
    .sel(opcode[1]), .in_0(multiplexer_1_out), .in_1(multiplexer_2_out), .out(multiplexer_8_out));
  Multiplexer #(.Bits(16)) multiplexer_9 (
    .sel(opcode[1]), .in_0(multiplexer_4_out), .in_1(multiplexer_5_out), .out(multiplexer_9_out));
  Multiplexer #(.Bits(16)) multiplexer_10 (
    .sel(opcode[1]), .in_0(multiplexer_6_out), .in_1(multiplexer_7_out), .out(multiplexer_10_out));
  Multiplexer #(.Bits(16)) multiplexer_11 (
    .sel(opcode[2]), .in_0(multiplexer_8_out), .in_1(multiplexer_3_out), .out(multiplexer_11_out));
  Multiplexer #(.Bits(16)) multiplexer_12 (
    .sel(opcode[2]), .in_0(multiplexer_9_out), .in_1(multiplexer_10_out), .out(multiplexer_12_out));
  Multiplexer #(.Bits(16)) multiplexer_13 (
    .sel(compare_1_p4), .in_0({16{1'b0}}), .in_1({16{1'b1}}), .out(multiplexer_13_out));
  Multiplexer #(.Bits(16)) multiplexer_14 (
    .sel(opcode[3]), .in_0(multiplexer_12_out), .in_1(multiplexer_13_out), .out(multiplexer_14_out));
  Multiplexer #(.Bits(16)) multiplexer_15 (
    .sel(opcode[4]), .in_0(multiplexer_11_out), .in_1(multiplexer_14_out), .out(Z));

  // Notes on the sheet:
  //   arithmetic
  //   logic
  //   comparison
endmodule

/* Test case procedural tests:
  opcode  X   Y   Z

loop(i,50)
  let x = random(0xFFFF);
  let y = random(0xFFFF);

  0b00000 (x) (y) (x+y) 
  0b00001 (x) (y) (x-y)
  0b00010 (x) (y) (x*y)
# division often fails because digital does not use signed division
#  0b00011 (x) (y) (x/y)
# shifting done separately with lower X

  0b10000 (x) (y) (x&y)
  0b10001 (x) (y) (x|y)
  0b10010 (x) (y) (~x)
# 0b10011
  0b10100 (x) (y) (x^y)
  0b10101 (x) (y) (~(x^y))
  0b10110 (x) (y) (~(x|y))
  0b10111 (x) (y) (~(x&y))

# comparison often fails because digital does not do signed comparisons
  0b11000 (x) (y) 0x0000
#  0b11001 (x) (y) (ite(x> y, 0xFFFF, 0x0000))
#  0b11010 (x) (y) (ite(x= y, 0xFFFF, 0x0000))
#  0b11011 (x) (y) (ite(x>=y, 0xFFFF, 0x0000))
#  0b11100 (x) (y) (ite(x< y, 0xFFFF, 0x0000))
#  0b11101 (x) (y) (ite(x!=y, 0xFFFF, 0x0000))
#  0b11110 (x) (y) (ite(x<=y, 0xFFFF, 0x0000))
  0b11111 (x) (y) 0xFFFF
end loop


loop(j,50)
  let x = random(0xFFFF);
  let y = random(16);

  0b00100 (x) (y) (x<<y)
  0b00101 (x) (y) (x>>y)
end loop
*/

/* Test case arithmetic:
opcode      X       Y       Z    remainder
# addition
0b00000  0x0000  0x0000  0x0000  x
0b00000  0x0001  0x0000  0x0001  x
0b00000  0x0000  0x0001  0x0001  x
0b00000  0x0001  0x0001  0x0002  x
0b00000  0x0002  0x0003  0x0005  x

# subtraction
0b00001  0x0000  0x0000  0x0000  x
0b00001  0x0001  0x0000  0x0001  x
0b00001  0x0001  0x0001  0x0000  x
0b00001  0x0002  0x0001  0x0001  x
0b00001  0x0002  0x0000  0x0002  x
0b00001  0x0001  0x0002  0xFFFF  x
0b00001  0x0000  0x0001  0xFFFF  x
0b00001  0x0000  0x0002  0xFFFE  x

# multiplication
0b00010  0x0000  0x0000  0x0000  x
0b00010  0x0001  0x0000  0x0000  x
0b00010  0x0000  0x0001  0x0000  x
0b00010  0x0001  0x0001  0x0001  x
0b00010  0x0000  0x0002  0x0000  x
0b00010  0x0002  0x0000  0x0000  x
0b00010  0x0002  0x0002  0x0004  x
0b00010  0x0002  0x0001  0x0002  x
0b00010  0x0001  0x0002  0x0002  x
0b00010  0xFFFF  0x0002  0xFFFE  x
0b00010  0x0002  0xFFFF  0xFFFE  x

# division
0b00011  0x0001  0x0001  0x0001  0
0b00011  0x0002  0x0001  0x0002  0
0b00011  0x0003  0x0001  0x0003  0
0b00011  0x0004  0x0001  0x0004  0
0b00011  0x0005  0x0001  0x0005  0
0b00011  0x0006  0x0001  0x0006  0
0b00011  0x0007  0x0001  0x0007  0

0b00011  0x0001  0x0002  0x0000  1
0b00011  0x0002  0x0002  0x0001  0
0b00011  0x0003  0x0002  0x0001  1
0b00011  0x0004  0x0002  0x0002  0
0b00011  0x0005  0x0002  0x0002  1
0b00011  0x0006  0x0002  0x0003  0
0b00011  0x0007  0x0002  0x0003  1

# shift left
0b00100  0x0000  0x0000  0x0000  x
0b00100  0x0000  0x0001  0x0000  x
0b00100  0x0000  0x0002  0x0000  x
0b00100  0x0001  0x0000  0x0001  x
0b00100  0x0001  0x0001  0x0002  x
0b00100  0x0001  0x0002  0x0004  x
0b00100  0x0002  0x0000  0x0002  x
0b00100  0x0002  0x0001  0x0004  x
0b00100  0x0002  0x0002  0x0008  x
0b00100  0x0003  0x0000  0x0003  x
0b00100  0x0003  0x0001  0x0006  x
0b00100  0x0003  0x0002  0x000C  x

# shift right
0b00101  0x0000  0x0000  0x0000  x
0b00101  0x0000  0x0001  0x0000  x
0b00101  0x0000  0x0002  0x0000  x
0b00101  0x0002  0x0000  0x0002  x
0b00101  0x0002  0x0001  0x0001  x
0b00101  0x0002  0x0002  0x0000  x
0b00101  0x0003  0x0000  0x0003  x
0b00101  0x0003  0x0001  0x0001  x
0b00101  0x0003  0x0002  0x0000  x
0b00101  0x0004  0x0000  0x0004  x
0b00101  0x0004  0x0001  0x0002  x
0b00101  0x0004  0x0002  0x0001  x
*/

/* Test case bitwise:
opcode   X       Y       Z
# bitwise and
0b10000  0x0000  0x0000  0x0000
0b10000  0x0000  0x0001  0x0000
0b10000  0x0001  0x0000  0x0000
0b10000  0x0001  0x0001  0x0001
0b10000  0x0002  0x0001  0x0000
0b10000  0x0001  0x0002  0x0000
0b10000  0x0002  0x0002  0x0002
0b10000  0x0002  0x0000  0x0000
0b10000  0x0000  0x0002  0x0000
0b10000  0x0003  0x0002  0x0002

# bitwise or
0b10001  0x0000  0x0000  0x0000
0b10001  0x0000  0x0001  0x0001
0b10001  0x0001  0x0000  0x0001
0b10001  0x0001  0x0001  0x0001
0b10001  0x0002  0x0001  0x0003
0b10001  0x0001  0x0002  0x0003
0b10001  0x0002  0x0002  0x0002
0b10001  0x0002  0x0000  0x0002
0b10001  0x0000  0x0002  0x0002
0b10001  0x0003  0x0002  0x0003

# bitwise not x
0b10010  0x0000  0x0000  0xFFFF
0b10010  0x0000  0x0001  0xFFFF
0b10010  0x0001  0x0000  0xFFFE
0b10010  0x0001  0x0001  0xFFFE
0b10010  0x0002  0x0000  0xFFFD
0b10010  0x0002  0x0001  0xFFFD
0b10010  0x0003  0x0000  0xFFFC
0b10010  0x0003  0x0001  0xFFFC
0b10010  0x0004  0x0000  0xFFFB
0b10010  0x0004  0x0001  0xFFFB

# bitwise not y
0b10011  0x0000  0x0000  0xFFFF
0b10011  0x0001  0x0000  0xFFFF
0b10011  0x0000  0x0001  0xFFFE
0b10011  0x0001  0x0001  0xFFFE
0b10011  0x0000  0x0002  0xFFFD
0b10011  0x0001  0x0002  0xFFFD
0b10011  0x0000  0x0003  0xFFFC
0b10011  0x0001  0x0003  0xFFFC
0b10011  0x0000  0x0004  0xFFFB
0b10011  0x0001  0x0004  0xFFFB

# bitwise xor
0b10100  0x0000  0x0000  0x0000
0b10100  0x0001  0x0000  0x0001
0b10100  0x0000  0x0001  0x0001
0b10100  0x0001  0x0001  0x0000
0b10100  0x0000  0x0002  0x0002
0b10100  0x0001  0x0002  0x0003
0b10100  0x0000  0x0003  0x0003
0b10100  0x0001  0x0003  0x0002
0b10100  0x0000  0x0004  0x0004

# bitwise xnor
0b10101  0x0000  0x0000  0xFFFF
0b10101  0x0001  0x0000  0xFFFE
0b10101  0x0000  0x0001  0xFFFE
0b10101  0x0001  0x0001  0xFFFF
0b10101  0x0000  0x0002  0xFFFD
0b10101  0x0001  0x0002  0xFFFC
0b10101  0x0000  0x0003  0xFFFC
0b10101  0x0001  0x0003  0xFFFD
0b10101  0x0000  0x0004  0xFFFB

# bitwise nor
0b10110  0x0000  0x0000  0xFFFF
0b10110  0x0001  0x0000  0xFFFE
0b10110  0x0000  0x0001  0xFFFE
0b10110  0x0001  0x0001  0xFFFE
0b10110  0x0000  0x0002  0xFFFD
0b10110  0x0001  0x0002  0xFFFC
0b10110  0x0000  0x0003  0xFFFC
0b10110  0x0001  0x0003  0xFFFC
0b10110  0x0000  0x0004  0xFFFB

# bitwise nand
0b10111  0x0000  0x0000  0xFFFF
0b10111  0x0001  0x0000  0xFFFF
0b10111  0x0000  0x0001  0xFFFF
0b10111  0x0001  0x0001  0xFFFE
0b10111  0x0000  0x0002  0xFFFF
0b10111  0x0001  0x0002  0xFFFF
0b10111  0x0000  0x0003  0xFFFF
0b10111  0x0001  0x0003  0xFFFE
0b10111  0x0000  0x0004  0xFFFF
*/

/* Test case comparison:
opcode   X       Y       Z
# false
0b11000  0x0000  0x0000  0x0000
0b11000  0x0000  0x0001  0x0000
0b11000  0x0001  0x0000  0x0000
0b11000  0x0001  0x0001  0x0000
0b11000  0x0002  0x0001  0x0000
0b11000  0x0001  0x0002  0x0000
0b11000  0x0002  0x0002  0x0000
0b11000  0x0002  0x0000  0x0000
0b11000  0x0000  0x0002  0x0000
0b11000  0x0003  0x0002  0x0000

# greater than
0b11001  0x0000  0x0000  0x0000
0b11001  0x0000  0x0001  0x0000
0b11001  0x0001  0x0000  0xFFFF
0b11001  0x0001  0x0001  0x0000
0b11001  0x0002  0x0001  0xFFFF
0b11001  0x0001  0x0002  0x0000
0b11001  0x0002  0x0002  0x0000
0b11001  0x0002  0x0000  0xFFFF
0b11001  0x0000  0x0002  0x0000
0b11001  0x0003  0x0002  0xFFFF

# equals
0b11010  0x0000  0x0000  0xFFFF
0b11010  0x0000  0x0001  0x0000
0b11010  0x0001  0x0000  0x0000
0b11010  0x0001  0x0001  0xFFFF
0b11010  0x0002  0x0001  0x0000
0b11010  0x0001  0x0002  0x0000
0b11010  0x0002  0x0002  0xFFFF
0b11010  0x0002  0x0000  0x0000
0b11010  0x0000  0x0002  0x0000
0b11010  0x0003  0x0002  0x0000

# greater than or equals
0b11011  0x0000  0x0000  0xFFFF
0b11011  0x0000  0x0001  0x0000
0b11011  0x0001  0x0000  0xFFFF
0b11011  0x0001  0x0001  0xFFFF
0b11011  0x0002  0x0001  0xFFFF
0b11011  0x0001  0x0002  0x0000
0b11011  0x0002  0x0002  0xFFFF
0b11011  0x0002  0x0000  0xFFFF
0b11011  0x0000  0x0002  0x0000
0b11011  0x0003  0x0002  0xFFFF

# less than
0b11100  0x0000  0x0000  0x0000
0b11100  0x0000  0x0001  0xFFFF
0b11100  0x0001  0x0000  0x0000
0b11100  0x0001  0x0001  0x0000
0b11100  0x0002  0x0001  0x0000
0b11100  0x0001  0x0002  0xFFFF
0b11100  0x0002  0x0002  0x0000
0b11100  0x0002  0x0000  0x0000
0b11100  0x0000  0x0002  0xFFFF
0b11100  0x0003  0x0002  0x0000

# less than or equals
0b11110  0x0000  0x0000  0xFFFF
0b11110  0x0000  0x0001  0xFFFF
0b11110  0x0001  0x0000  0x0000
0b11110  0x0001  0x0001  0xFFFF
0b11110  0x0002  0x0001  0x0000
0b11110  0x0001  0x0002  0xFFFF
0b11110  0x0002  0x0002  0xFFFF
0b11110  0x0002  0x0000  0x0000
0b11110  0x0000  0x0002  0xFFFF
0b11110  0x0003  0x0002  0x0000

# not equals
0b11101  0x0000  0x0000  0x0000
0b11101  0x0000  0x0001  0xFFFF
0b11101  0x0001  0x0000  0xFFFF
0b11101  0x0001  0x0001  0x0000
0b11101  0x0002  0x0001  0xFFFF
0b11101  0x0001  0x0002  0xFFFF
0b11101  0x0002  0x0002  0x0000
0b11101  0x0002  0x0000  0xFFFF
0b11101  0x0000  0x0002  0xFFFF
0b11101  0x0003  0x0002  0xFFFF

# true
0b11111  0x0000  0x0000  0xFFFF
0b11111  0x0000  0x0001  0xFFFF
0b11111  0x0001  0x0000  0xFFFF
0b11111  0x0001  0x0001  0xFFFF
0b11111  0x0002  0x0001  0xFFFF
0b11111  0x0001  0x0002  0xFFFF
0b11111  0x0002  0x0002  0xFFFF
0b11111  0x0002  0x0000  0xFFFF
0b11111  0x0000  0x0002  0xFFFF
0b11111  0x0003  0x0002  0xFFFF
*/
