// Digital circuit alu_operands.dig as structural Verilog
module alu_operands (
  input  [1:0] Xsel,
  input  [1:0] Ysel,
  input  [15:0] a,
  input  [15:0] b,
  input  [15:0] c,
  input  [15:0] d,
  output [15:0] X,
  output [15:0] Y
);

  Multiplexer #(.Selector_Bits(2), .Bits(16)) multiplexer_1 (
    .sel(Xsel), .in_0(a), .in_1(b), .in_2(c), .in_3(d), .out(X));
  Multiplexer #(.Selector_Bits(2), .Bits(16)) multiplexer_2 (
    .sel(Ysel), .in_0(a), .in_1(b), .in_2(c), .in_3(d), .out(Y));
endmodule

/* Test case tests:
    Xsel Ysel a   b   c   d   X   Y

loop(m,4)
  loop(i,5)
    let a = random(0xffff);
    let b = random(0xffff);
    let c = random(0xffff);
    let d = random(0xffff);
    
    0b00 0b00 (a) (b) (c) (d) (a) (a)
    0b00 0b01 (a) (b) (c) (d) (a) (b)
    0b00 0b10 (a) (b) (c) (d) (a) (c)
    0b00 0b11 (a) (b) (c) (d) (a) (d)

    0b01 0b00 (a) (b) (c) (d) (b) (a)
    0b01 0b01 (a) (b) (c) (d) (b) (b)
    0b01 0b10 (a) (b) (c) (d) (b) (c)
    0b01 0b11 (a) (b) (c) (d) (b) (d)

    0b10 0b00 (a) (b) (c) (d) (c) (a)
    0b10 0b01 (a) (b) (c) (d) (c) (b)
    0b10 0b10 (a) (b) (c) (d) (c) (c)
    0b10 0b11 (a) (b) (c) (d) (c) (d)

    0b11 0b00 (a) (b) (c) (d) (d) (a)
    0b11 0b01 (a) (b) (c) (d) (d) (b)
    0b11 0b10 (a) (b) (c) (d) (d) (c)
    0b11 0b11 (a) (b) (c) (d) (d) (d)
  end loop
end loop
*/
