// Digital circuit bus_driver.dig as structural Verilog
module bus_driver (
  input  [15:0] iout,
  input  ie,
  input  [15:0] iaddr,
  output [15:0] oaddr,
  output oe,
  output [15:0] oout
);

  assign oaddr = ie ? iaddr : 16'bz;  // Driver driver_1
  assign oout = ie ? iout : 16'bz;  // Driver driver_2

  assign oe = ie;
endmodule
