// Digital circuit cpu_proc16b1.dig as structural Verilog
module cpu_proc16b1 (
  input  [15:0] inst,
  input  [15:0] bus_in,
  input  clock,
  output [15:0] ptr_inst,
  output [15:0] bus_addr,
  output [15:0] bus_out,
  output bus_write,
  output \break 
);

  wire and_1_out, and_2_out, and_3_out, and_4_out, and_5_out, and_6_out, and_7_out, and_8_out, and_9_out,
       and_10_out, and_11_out, and_12_out, jump_success, mode_alu, mode_constant, mode_jump, mode_noop,
       mode_readwrite, read_a, read_b, read_bus, read_c, read_d, read_o, read_r, write_a, write_b, write_bus,
       write_c, write_d, write_enable, write_overflow;
  wire [1:0] alu_x, alu_y, jump_tgt, jump_x, jump_y;
  wire [2:0] bus_address_sel, decoder_1_mode, jump_cmp;
  wire [4:0] alu_op;
  wire [15:0] add_1_s, alu_1_z, alu_operands_1_x, alu_operands_1_y, alu_operands_2_x, alu_operands_2_y,
       constant_value, multiplexer_1_out, reg_a, reg_b, reg_c, reg_d, reg_o, reg_r, write_pc, write_remainder;

  and and_1 (and_1_out, write_a, write_enable);
  and and_2 (and_2_out, write_b, write_enable);
  and and_3 (and_3_out, write_c, write_enable);
  and and_4 (and_4_out, write_d, write_enable);
  decoder decoder_1 (
    .instruction(inst), .mode(decoder_1_mode), .constant_value(constant_value), .alu_x(alu_x), .alu_y(alu_y),
    .alu_op(alu_op), .jump_x(jump_x), .jump_y(jump_y), .jump_tgt(jump_tgt), .jump_cmp(jump_cmp),
    .bus_address(bus_address_sel), .read_a(read_a), .read_b(read_b), .read_c(read_c), .read_d(read_d),
    .read_bus(read_bus), .read_o(read_o), .read_r(read_r), .write_enable(write_enable), .write_a(write_a),
    .write_b(write_b), .write_c(write_c), .write_d(write_d), .write_bus(write_bus));
  Register #(.Bits(16)) A (.D(bus_out), .C(clock), .en(and_1_out), .Q(reg_a));
  Register #(.Bits(16)) B (.D(bus_out), .C(clock), .en(and_2_out), .Q(reg_b));
  Register #(.Bits(16)) C (.D(bus_out), .C(clock), .en(and_3_out), .Q(reg_c));
  Register #(.Bits(16)) D (.D(bus_out), .C(clock), .en(and_4_out), .Q(reg_d));
  Register #(.Bits(16)) o (.D({{15{1'b0}}, write_overflow}), .C(clock), .en(mode_alu), .Q(reg_o));
  Register #(.Bits(16)) r (.D(write_remainder), .C(clock), .en(mode_alu), .Q(reg_r));
  Register #(.Bits(16)) PC (.D(write_pc), .C(clock), .en(1'b1), .Q(ptr_inst));
  // Probe reg_a on reg_a
  // Probe reg_b on reg_b
  // Probe reg_c on reg_c
  // Probe reg_d on reg_d
  // Probe reg_o on reg_o
  // Probe reg_r on reg_r
  // Probe reg_pc on ptr_inst
  Demultiplexer #(.Selector_Bits(3)) demultiplexer_1 (
    .sel(decoder_1_mode), .in(1'b1), .out_0(mode_constant), .out_1(mode_alu), .out_2(mode_jump),
    .out_3(mode_readwrite), .out_4(mode_noop), .out_5(\break ));  // open: out_6, out_7
  Multiplexer #(.Selector_Bits(2), .Bits(16)) multiplexer_1 (
    .sel(jump_tgt), .in_0(reg_a), .in_1(reg_b), .in_2(reg_c), .in_3(reg_d), .out(multiplexer_1_out));
  alu_operands alu_operands_1 (
    .Xsel(jump_x), .Ysel(jump_y), .a(reg_a), .b(reg_b), .c(reg_c), .d(reg_d), .X(alu_operands_1_x),
    .Y(alu_operands_1_y));
  Add #(.Bits(16)) add_1 (.a(ptr_inst), .b(16'h1), .c_i(1'b0), .s(add_1_s));  // open: c_o
  and and_5 (and_5_out, mode_jump, jump_success);
  Multiplexer #(.Bits(16)) multiplexer_2 (.sel(and_5_out), .in_0(add_1_s), .in_1(multiplexer_1_out), .out(write_pc));
  // compare compare_1: pin names not known; wires that end beside it: alu_operands_1_x, alu_operands_1_y, jump_cmp, jump_success
  alu_operands alu_operands_2 (
    .Xsel(alu_x), .Ysel(alu_y), .a(reg_a), .b(reg_b), .c(reg_c), .d(reg_d), .X(alu_operands_2_x),
    .Y(alu_operands_2_y));
  alu alu_1 (
    .opcode(alu_op), .X(alu_operands_2_x), .Y(alu_operands_2_y), .Z(alu_1_z), .remainder(write_remainder),
    .overflow(write_overflow));
  assign bus_out = mode_alu ? alu_1_z : 16'bz;  // Driver driver_1
  and and_6 (and_6_out, read_a, mode_readwrite);
  and and_7 (and_7_out, read_b, mode_readwrite);
  and and_8 (and_8_out, read_c, mode_readwrite);
  and and_9 (and_9_out, read_d, mode_readwrite);
  and and_10 (and_10_out, read_o, mode_readwrite);
  and and_11 (and_11_out, read_r, mode_readwrite);
  and and_12 (and_12_out, read_bus, mode_readwrite);
  assign bus_out = mode_constant ? constant_value : 16'bz;  // Driver driver_2
  assign bus_out = and_6_out ? reg_a : 16'bz;  // Driver driver_3
  assign bus_out = and_7_out ? reg_b : 16'bz;  // Driver driver_4
  assign bus_out = and_8_out ? reg_c : 16'bz;  // Driver driver_5
  assign bus_out = and_9_out ? reg_d : 16'bz;  // Driver driver_6
  assign bus_out = and_10_out ? reg_o : 16'bz;  // Driver driver_7
  assign bus_out = and_11_out ? reg_r : 16'bz;  // Driver driver_8
  assign bus_out = and_12_out ? bus_in : 16'bz;  // Driver driver_9
  // Probe write_val on bus_out
  Multiplexer #(.Selector_Bits(2), .Bits(16)) multiplexer_3 (
    .sel(bus_address_sel[1:0]), .in_0(reg_a), .in_1(reg_b), .in_2(reg_c), .in_3(reg_d), .out(bus_addr));
  and and_13 (bus_write, write_bus, mode_readwrite);

  // Other names for the same wires on the sheet: mode_break = \break ; reg_pc[15:0] = ptr_inst;
  //   write_val[15:0] = bus_out

  // Notes on the sheet:
  //   input/decoder
  //   registers
  //   program counter manager
  //   jump
  //   alu
  //   read/write
  //   output
endmodule

/* Test case ldc tests:
clock inst  bus_in  reg_a  reg_b  reg_c  reg_d  reg_o  reg_r
C  0b0000000000000001  0   1  0  0  0  0  0
C  0b0000000000000010  0   2  0  0  0  0  0
C  0b0001000000000011  0   2  3  0  0  0  0
C  0b0010000000000100  0   2  3  4  0  0  0
C  0b0011000000000101  0   2  3  4  5  0  0
*/

/* Test case alu tests:
clock inst  reg_a  reg_b  reg_c  reg_d  reg_r
# ldc %a, $1
C  0b0000000000000001  1  0  0  0  x
# ldc %b, $2
C  0b0001000000000010  1  2  0  0  x

# add %c, %a, %b
#    01xxyywwooooo___
C  0b0100011000000000  1  2  3  0  x

# sub %c, %b, %a
C  0b0101001000001000  1  2  1  0  x

# div %c, %a, %b
C  0b0100011000011000  1  2  0  0  1
*/

/* Test case jump tests:
clock  inst  reg_a  reg_b  reg_c  reg_d  reg_pc

# note: clock/reg_pc weirdness
# if you use a C signal in Digital, it first sets all the inputs, then pulses the clock, and then compares the outputs.
# the result of this is that the reg_pc probe is always the instruction pointer that the cpu wants NEXT.
# so, if you run the first test line and pulse the clock right away, reg_pc should be 1. it was 0 before the clock pulse.
# but if you execute a jump to 0, then the reg_pc will be 0. because that's the instruction that it wants next.
# it's a little unintuitive to me. maybe it isn't to you.

# ldc %a, $1
#    00rrvvvvvvvvvvvv
C  0b0000000000000001  1  0  0  0  1

# ldc %b, $2
C  0b0001000000000010  1  2  0  0  2

# ldc %d, $0xFF
C  0b0011000011111111  1  2  0  0xFF 3

# jgt %c, %a, %b (jump to c if a > b) (it's not)
#    100xxyyttccc____
C  0b1000001100010000  1  2  0  0xFF  4

# jlt %c, %a, %b (jump to c if a < b) (it is)
#    100xxyyttccc____
C  0b1000001101000000  1  2  0  0xFF  0

# jlt %d, %a, %b (jump to d if a < b) (it is)
#    100xxyyttccc____
C  0b1000001111000000  1  2  0  0xFF  0xFF

# jump to c if false
#    100xxyyttccc____
C  0b1000001100000000  1  2  0  0xFF  0x100

# jmp %c (jump to c if true)
#    100xxyyttccc____
C  0b1000001101110000  1  2  0  0xFF  0
*/

/* Test case rw tests:
clock  inst          bus_in  reg_a  reg_b  reg_c  reg_d  reg_o  reg_r  bus_write  bus_addr  bus_out

# set up some values in registers
# o=0, r=1, a=2, b=3, c=4, d=5

# ldc %a, $2
C 0b0000000000000010 0x0000  0x0002 0x0000 0x0000 0x0000 0x0000 0x0000 0 x      x
# ldc %b, $3
C 0b0001000000000011 0x0000  0x0002 0x0003 0x0000 0x0000 0x0000 0x0000 0 x      x
# ldc %c, $4
C 0b0010000000000100 0x0000  0x0002 0x0003 0x0004 0x0000 0x0000 0x0000 0 x      x
# ldc %d, $5
C 0b0011000000000101 0x0000  0x0002 0x0003 0x0004 0x0005 0x0000 0x0000 0 x      x
# div %a, %d, %a (a = 5 / 2) a = 2, r = 1
#   01xxyywwooooo___
C 0b0111000000011000 0x0000  0x0002 0x0003 0x0004 0x0005 0x0000 0x0001 0 x      x

# stb %a, %b (*a = b)
#   1011maaavvv_____
C 0b1011100000100000 0x0000  0x0002 0x0003 0x0004 0x0005 0x0000 0x0001 1 0x0002 0x0003

# stb %c, %d (*c = d)
C 0b1011101001100000 0x0000  0x0002 0x0003 0x0004 0x0005 0x0000 0x0001 1 0x0004 0x0005

# ldb %a, %b (b = *a)
C 0b1011000000100000 0x0006  0x0002 0x0006 0x0004 0x0005 0x0000 0x0001 0 0x0002 x

# ldb %c, %a (a = *c)
C 0b1011001000000000 0x0007  0x0007 0x0006 0x0004 0x0005 0x0000 0x0001 0 0x0004 x
*/

/* Test case misc tests:
clock  inst  ptr_inst  bus_write  break
# noop
#   111_----____----
0 0b1110000000000000 0  0  0
# brk
C 0b1110000000000001 1  0  1
C 0b1110000000000000 2  0  0
C 0b1110000000000001 3  0  1
*/

/* Test case ramfill test:
clock inst            reg_a  reg_b  reg_c  reg_d  ptr_inst bus_addr bus_out bus_write
C 0b0000000000000000  0x0000 0x0000 0x0000 0x0000 0x0001   x        x       0
C 0b0001000000000000  0x0000 0x0000 0x0000 0x0000 0x0002   x        x       0
C 0b0010000000000001  0x0000 0x0000 0x0001 0x0000 0x0003   x        x       0

# loop block
C 0b0011000000000010  0x0000 0x0000 0x0001 0x0002 0x0004   x        x       0
C 0b0100100000000000  0x0001 0x0000 0x0001 0x0002 0x0005   x        x       0
C 0b0100110100010000  0x0001 0x0002 0x0001 0x0002 0x0006   x        x       0
C 0b1011100000100000  0x0001 0x0002 0x0001 0x0002 0x0007   0x0001   0x0002  1
C 0b0011000000000011  0x0001 0x0002 0x0001 0x0003 0x0008   x        x       0
C 0b1000000111110000  0x0001 0x0002 0x0001 0x0003 0x0003   x        x       0

# see note in "jump tests"
C 0b0011000000000010  0x0001 0x0002 0x0001 0x0002 0x0004   x        x       0
C 0b0100100000000000  0x0002 0x0002 0x0001 0x0002 0x0005   x        x       0
C 0b0100110100010000  0x0002 0x0004 0x0001 0x0002 0x0006   x        x       0
C 0b1011100000100000  0x0002 0x0004 0x0001 0x0002 0x0007   0x0002   0x0004  1
C 0b0011000000000011  0x0002 0x0004 0x0001 0x0003 0x0008   x        x       0
C 0b1000000111110000  0x0002 0x0004 0x0001 0x0003 0x0003   x        x       0


C 0b0011000000000010  0x0002 0x0004 0x0001 0x0002 0x0004   x        x       0
C 0b0100100000000000  0x0003 0x0004 0x0001 0x0002 0x0005   x        x       0
C 0b0100110100010000  0x0003 0x0006 0x0001 0x0002 0x0006   x        x       0
C 0b1011100000100000  0x0003 0x0006 0x0001 0x0002 0x0007   0x0003   0x0006  1
C 0b0011000000000011  0x0003 0x0006 0x0001 0x0003 0x0008   x        x       0
C 0b1000000111110000  0x0003 0x0006 0x0001 0x0003 0x0003   x        x       0


C 0b0011000000000010  0x0003 0x0006 0x0001 0x0002 0x0004   x        x       0
C 0b0100100000000000  0x0004 0x0006 0x0001 0x0002 0x0005   x        x       0
C 0b0100110100010000  0x0004 0x0008 0x0001 0x0002 0x0006   x        x       0
C 0b1011100000100000  0x0004 0x0008 0x0001 0x0002 0x0007   0x0004   0x0008  1
C 0b0011000000000011  0x0004 0x0008 0x0001 0x0003 0x0008   x        x       0
C 0b1000000111110000  0x0004 0x0008 0x0001 0x0003 0x0003   x        x       0
*/

/* Test case increment test:
clock inst            reg_a  reg_b  reg_c  reg_d  ptr_inst bus_write
C 0b0000000000000000  0x0000 0x0000 0x0000 0x0000 0x0001   0
C 0b0001000000000001  0x0000 0x0001 0x0000 0x0000 0x0002   0
C 0b0010000000000011  0x0000 0x0001 0x0003 0x0000 0x0003   0

C 0b0100010000000000  0x0001 0x0001 0x0003 0x0000 0x0004   0
C 0b1000000101110000  0x0001 0x0001 0x0003 0x0000 0x0003   0

C 0b0100010000000000  0x0002 0x0001 0x0003 0x0000 0x0004   0
C 0b1000000101110000  0x0002 0x0001 0x0003 0x0000 0x0003   0

C 0b0100010000000000  0x0003 0x0001 0x0003 0x0000 0x0004   0
C 0b1000000101110000  0x0003 0x0001 0x0003 0x0000 0x0003   0

C 0b0100010000000000  0x0004 0x0001 0x0003 0x0000 0x0004   0
C 0b1000000101110000  0x0004 0x0001 0x0003 0x0000 0x0003   0

C 0b0100010000000000  0x0005 0x0001 0x0003 0x0000 0x0004   0
C 0b1000000101110000  0x0005 0x0001 0x0003 0x0000 0x0003   0

C 0b0100010000000000  0x0006 0x0001 0x0003 0x0000 0x0004   0
C 0b1000000101110000  0x0006 0x0001 0x0003 0x0000 0x0003   0

C 0b0100010000000000  0x0007 0x0001 0x0003 0x0000 0x0004   0
C 0b1000000101110000  0x0007 0x0001 0x0003 0x0000 0x0003   0
*/

/* Test case fibonacci tests:
clock inst bus_in  reg_a  reg_b  reg_c  reg_d  ptr_inst bus_addr bus_out bus_write
C   0x0001 0xFFFF  0x0001 x      x      x      0x0001   x        x       0
C   0xb800 0xFFFF  0x0001 x      x      x      0x0002   0x0001   0x0001  1
C   0x0002 0xFFFF  0x0002 x      x      x      0x0003   x        x       0
C   0xb800 0xFFFF  0x0002 x      x      x      0x0004   0x0002   0x0002  1
C   0x1000 0xFFFF  0x0002 0x0000 x      x      0x0005   x        x       0
C   0xb900 0xFFFF  0x0002 0x0000 x      x      0x0006   0x0000   0x0002  1
C   0x0001 0xFFFF  0x0001 0x0000 x      x      0x0007   x        x       0
C   0x3001 0xFFFF  0x0001 0x0000 x      0x0001 0x0008   x        x       0
#C   0xb360 0x0000  0x0001 0x0000 x      0x0001 0x0009   0x0001   x       0
*/

/* Test case short regression 1:
# 0xA100 was found to be able to cause a short. however, it is a legal instruction.
# this is non deterministic.
# adding repeated 0xA100 instructions does not seem to increase the chance of it happening,
# but resetting the registers every time does.

clock inst  reg_a  reg_b

loop(a,10)
  C  0x0000   0      x
  C  0x1004   0      4
  C  0xA100   4      4
end loop
*/
