// Digital circuit decoder.dig as structural Verilog
module decoder (
  input  [15:0] instruction,
  output write_a,
  output write_b,
  output write_c,
  output write_d,
  output [4:0] alu_op,
  output [1:0] alu_y,
  output [1:0] alu_x,
  output [15:0] constant_value,
  output [1:0] jump_tgt,
  output [1:0] jump_y,
  output [1:0] jump_x,
  output write_bus,
  output read_a,
  output read_b,
  output read_c,
  output read_d,
  output read_bus,
  output read_o,
  output read_r,
  output [2:0] mode,
  output [2:0] jump_cmp,
  output [2:0] bus_address,
  output write_enable
);

  wire demultiplexer_2_out_1, demultiplexer_3_out_0, demultiplexer_3_out_1, demultiplexer_3_out_2,
       demultiplexer_3_out_3, demultiplexer_4_out_0, demultiplexer_4_out_1, demultiplexer_4_out_2,
       demultiplexer_4_out_3, demultiplexer_5_out_0, demultiplexer_5_out_1, demultiplexer_5_out_2,
       demultiplexer_5_out_3, demultiplexer_5_out_4, demultiplexer_5_out_6, demultiplexer_5_out_8,
       demultiplexer_5_out_9, demultiplexer_6_out_0, demultiplexer_6_out_1, demultiplexer_6_out_2,
       demultiplexer_6_out_3, demultiplexer_7_out_0, demultiplexer_7_out_1, demultiplexer_7_out_2,
       demultiplexer_7_out_3, demultiplexer_8_out_0, demultiplexer_8_out_1, demultiplexer_8_out_2,
       demultiplexer_8_out_3, enable_alu, enable_bus, enable_constant, enable_jump, enable_misc, enable_mov,
       not_1_out, not_2_out, not_3_out;
  wire [2:0] multiplexer_1_out;

  Demultiplexer demultiplexer_1 (.sel(instruction[14]), .in(not_1_out), .out_0(enable_constant), .out_1(enable_alu));
  not not_1 (not_1_out, instruction[15]);
  Demultiplexer #(.Selector_Bits(2)) demultiplexer_2 (
    .sel(instruction[14:13]), .in(instruction[15]), .out_0(enable_jump), .out_1(demultiplexer_2_out_1),
    .out_3(enable_misc));  // open: out_2
  assign constant_value[11:0] = enable_constant ? instruction[11:0] : 12'bz;  // Driver driver_1
  Demultiplexer #(.Selector_Bits(2)) demultiplexer_3 (
    .sel(instruction[9:8]), .in(1'b1), .out_0(demultiplexer_3_out_0), .out_1(demultiplexer_3_out_1),
    .out_2(demultiplexer_3_out_2), .out_3(demultiplexer_3_out_3));
  assign write_enable = enable_jump ? 1'b0 : 1'bz;  // Driver driver_2
  Multiplexer #(.Bits(3)) multiplexer_1 (.sel(instruction[0]), .in_0(3'b100), .in_1(3'b101), .out(multiplexer_1_out));
  Demultiplexer #(.Selector_Bits(2)) demultiplexer_4 (
    .sel(instruction[13:12]), .in(1'b1), .out_0(demultiplexer_4_out_0), .out_1(demultiplexer_4_out_1),
    .out_2(demultiplexer_4_out_2), .out_3(demultiplexer_4_out_3));
  Demultiplexer #(.Selector_Bits(4)) demultiplexer_5 (
    .sel(instruction[11:8]), .in(1'b1), .out_0(demultiplexer_5_out_0), .out_1(demultiplexer_5_out_1),
    .out_2(demultiplexer_5_out_2), .out_3(demultiplexer_5_out_3), .out_4(demultiplexer_5_out_4),
    .out_6(demultiplexer_5_out_6), .out_8(demultiplexer_5_out_8), .out_9(demultiplexer_5_out_9));  // open: out_5, out_7, out_10, out_11, out_12, out_13, out_14, out_15
  not not_2 (not_2_out, instruction[11]);
  not not_3 (not_3_out, instruction[11]);
  assign write_enable = enable_misc ? 1'b0 : 1'bz;  // Driver driver_3
  assign mode = enable_misc ? multiplexer_1_out : 3'bz;  // Driver driver_4
  assign write_enable = enable_alu ? 1'b1 : 1'bz;  // Driver driver_5
  assign write_a = enable_alu ? demultiplexer_3_out_0 : 1'bz;  // Driver driver_6
  assign write_b = enable_alu ? demultiplexer_3_out_1 : 1'bz;  // Driver driver_7
  assign write_c = enable_alu ? demultiplexer_3_out_2 : 1'bz;  // Driver driver_8
  assign write_d = enable_alu ? demultiplexer_3_out_3 : 1'bz;  // Driver driver_9
  assign write_bus = enable_alu ? 1'b0 : 1'bz;  // Driver driver_10
  Demultiplexer #(.Selector_Bits(2)) demultiplexer_6 (
    .sel(instruction[6:5]), .in(instruction[11]), .out_0(demultiplexer_6_out_0),
    .out_1(demultiplexer_6_out_1), .out_2(demultiplexer_6_out_2), .out_3(demultiplexer_6_out_3));
  Demultiplexer #(.Selector_Bits(2)) demultiplexer_7 (
    .sel(instruction[6:5]), .in(not_2_out), .out_0(demultiplexer_7_out_0), .out_1(demultiplexer_7_out_1),
    .out_2(demultiplexer_7_out_2), .out_3(demultiplexer_7_out_3));
  assign mode = enable_constant ? 3'b000 : 3'bz;  // Driver driver_11
  assign mode = enable_alu ? 3'b001 : 3'bz;  // Driver driver_12
  assign mode = enable_jump ? 3'b010 : 3'bz;  // Driver driver_13
  assign write_enable = enable_constant ? 1'b1 : 1'bz;  // Driver driver_14
  assign write_a = enable_constant ? demultiplexer_4_out_0 : 1'bz;  // Driver driver_15
  assign write_b = enable_constant ? demultiplexer_4_out_1 : 1'bz;  // Driver driver_16
  assign write_c = enable_constant ? demultiplexer_4_out_2 : 1'bz;  // Driver driver_17
  assign write_d = enable_constant ? demultiplexer_4_out_3 : 1'bz;  // Driver driver_18
  assign write_bus = enable_constant ? 1'b0 : 1'bz;  // Driver driver_19
  Demultiplexer #(.Selector_Bits(2)) demultiplexer_8 (
    .sel(instruction[6:5]), .in(1'b1), .out_0(demultiplexer_8_out_0), .out_1(demultiplexer_8_out_1),
    .out_2(demultiplexer_8_out_2), .out_3(demultiplexer_8_out_3));
  assign read_a = enable_bus ? demultiplexer_6_out_0 : 1'bz;  // Driver driver_20
  assign read_b = enable_bus ? demultiplexer_6_out_1 : 1'bz;  // Driver driver_21
  assign read_c = enable_bus ? demultiplexer_6_out_2 : 1'bz;  // Driver driver_22
  assign read_d = enable_bus ? demultiplexer_6_out_3 : 1'bz;  // Driver driver_23
  assign write_a = enable_bus ? demultiplexer_7_out_0 : 1'bz;  // Driver driver_24
  assign write_b = enable_bus ? demultiplexer_7_out_1 : 1'bz;  // Driver driver_25
  assign write_c = enable_bus ? demultiplexer_7_out_2 : 1'bz;  // Driver driver_26
  assign write_d = enable_bus ? demultiplexer_7_out_3 : 1'bz;  // Driver driver_27
  assign read_bus = enable_bus ? not_3_out : 1'bz;  // Driver driver_28
  assign write_bus = enable_bus ? instruction[11] : 1'bz;  // Driver driver_29
  assign write_enable = enable_bus ? 1'b1 : 1'bz;  // Driver driver_30
  assign read_r = enable_bus ? 1'b0 : 1'bz;  // Driver driver_31
  assign read_o = enable_bus ? 1'b0 : 1'bz;  // Driver driver_32
  Demultiplexer demultiplexer_9 (
    .sel(instruction[12]), .in(demultiplexer_2_out_1), .out_0(enable_mov), .out_1(enable_bus));
  assign read_a = enable_mov ? demultiplexer_5_out_0 : 1'bz;  // Driver driver_33
  assign read_b = enable_mov ? demultiplexer_5_out_1 : 1'bz;  // Driver driver_34
  assign read_c = enable_mov ? demultiplexer_5_out_2 : 1'bz;  // Driver driver_35
  assign read_d = enable_mov ? demultiplexer_5_out_3 : 1'bz;  // Driver driver_36
  assign read_r = enable_mov ? demultiplexer_5_out_8 : 1'bz;  // Driver driver_37
  assign read_o = enable_mov ? demultiplexer_5_out_9 : 1'bz;  // Driver driver_38
  assign read_bus = enable_mov ? 1'b0 : 1'bz;  // Driver driver_39
  assign write_enable = enable_mov ? 1'b1 : 1'bz;  // Driver driver_40
  assign write_a = enable_mov ? demultiplexer_8_out_0 : 1'bz;  // Driver driver_41
  assign write_b = enable_mov ? demultiplexer_8_out_1 : 1'bz;  // Driver driver_42
  assign write_c = enable_mov ? demultiplexer_8_out_2 : 1'bz;  // Driver driver_43
  assign write_d = enable_mov ? demultiplexer_8_out_3 : 1'bz;  // Driver driver_44
  assign write_bus = enable_mov ? 1'b0 : 1'bz;  // Driver driver_45
  assign mode = enable_mov ? 3'b011 : 3'bz;  // Driver driver_46
  assign mode = enable_bus ? 3'b011 : 3'bz;  // Driver driver_47
  // Probe enable_constant on enable_constant
  // Probe enable_alu on enable_alu
  // Probe enable_jump on enable_jump
  // Probe enable_mov on enable_mov
  // Probe enable_bus on enable_bus
  // Probe enable_misc on enable_misc

  assign alu_op = instruction[7:3];
  assign alu_x = instruction[13:12];
  assign alu_y = instruction[11:10];
  assign bus_address = instruction[10:8];
  assign constant_value[15:12] = 4'b0000;
  assign jump_cmp = instruction[6:4];
  assign jump_tgt = instruction[8:7];
  assign jump_x = instruction[12:11];
  assign jump_y = instruction[10:9];

  // Notes on the sheet:
  //   mode: 000 constant
  //   001 alu
  //   010 jump
  //   011 read/write
  //   100 noop
  //   101 break
  //   mode
  //   constant
  //   alu
  //   jump
  //   mov
  //   bus
  //   misc
  //   output
endmodule

/* Test case mode tests:
instruction  mode  enable_constant  enable_alu  enable_jump  enable_mov  enable_bus  enable_misc
# ldc
0b0000000000000000  0b000  1  0  0  0  0  0
# alu
0b0100000000000000  0b001  0  1  0  0  0  0

# jump
0b1000000000000000  0b010  0  0  1  0  0  0

# mov
0b1010000000000000  0b011  0  0  0  1  0  0

# bus
0b1011000000000000  0b011  0  0  0  0  1  0

# misc (todo)
#0b1110000000000000  0b100  0  0  0  0  0  1
*/

/* Test case ldc tests:
instruction  mode  constant_value  write_a  write_b  write_c  write_d  write_bus
# 00rrvvvvvvvvvvvv
0b0000000000000000  0b000  0b000000000000  1  0  0  0  0
0b0001000000000000  0b000  0b000000000000  0  1  0  0  0
0b0010000000000000  0b000  0b000000000000  0  0  1  0  0
0b0011000000000000  0b000  0b000000000000  0  0  0  1  0

0b0000101010000001  0b000  0b101010000001  1  0  0  0  0
0b0001101010000001  0b000  0b101010000001  0  1  0  0  0
0b0010101010000001  0b000  0b101010000001  0  0  1  0  0
0b0011101010000001  0b000  0b101010000001  0  0  0  1  0
*/

/* Test case alu tests:
instruction  mode  alu_x  alu_y   alu_op  write_a  write_b  write_c  write_d  write_bus
# 01xxyywwooooonnn
0b0100000000000000  0b001  0b00  0b00  0b00000  1  0  0  0  0
0b0100000100000000  0b001  0b00  0b00  0b00000  0  1  0  0  0
0b0100001000000000  0b001  0b00  0b00  0b00000  0  0  1  0  0
0b0100001100000000  0b001  0b00  0b00  0b00000  0  0  0  1  0

0b0100010000000000  0b001  0b00  0b01  0b00000  1  0  0  0  0
0b0100100100000000  0b001  0b00  0b10  0b00000  0  1  0  0  0
0b0101001000000000  0b001  0b01  0b00  0b00000  0  0  1  0  0
0b0110001100000000  0b001  0b10  0b00  0b00000  0  0  0  1  0

0b0100010010000000  0b001  0b00  0b01  0b10000  1  0  0  0  0
0b0100100100100000  0b001  0b00  0b10  0b00100  0  1  0  0  0
0b0101001000110000  0b001  0b01  0b00  0b00110  0  0  1  0  0
0b0110001100001000  0b001  0b10  0b00  0b00001  0  0  0  1  0
*/

/* Test case jump tests:
instruction  mode  jump_x  jump_y  jump_tgt  jump_cmp
# 100xxyyttcccnnnn
0b1000000000000000  0b010  0b00  0b00  0b00  0b000

0b1001000000000000  0b010  0b10  0b00  0b00  0b000
0b1000100000000000  0b010  0b01  0b00  0b00  0b000
0b1000010000000000  0b010  0b00  0b10  0b00  0b000
0b1000001000000000  0b010  0b00  0b01  0b00  0b000

0b1001000000000000  0b010  0b10  0b00  0b00  0b000
0b1001100000000000  0b010  0b11  0b00  0b00  0b000
0b1000011000000000  0b010  0b00  0b11  0b00  0b000
0b1000001000000000  0b010  0b00  0b01  0b00  0b000

0b1001000100000000  0b010  0b10  0b00  0b10  0b000
0b1001100010000000  0b010  0b11  0b00  0b01  0b000
0b1000011110000000  0b010  0b00  0b11  0b11  0b000
0b1000001000000000  0b010  0b00  0b01  0b00  0b000

0b1001000101000000  0b010  0b10  0b00  0b10  0b100
0b1001100010100000  0b010  0b11  0b00  0b01  0b010
0b1000011110010000  0b010  0b00  0b11  0b11  0b001
0b1000001000110000  0b010  0b00  0b01  0b00  0b011
0b1000001001100000  0b010  0b00  0b01  0b00  0b110
0b1000001001110000  0b010  0b00  0b01  0b00  0b111
*/

/* Test case mov tests:
instruction  mode  read_a  read_b  read_c  read_d  read_r  read_o  read_bus  write_a  write_b  write_c  write_d  write_bus
# 1010sssstttnnnnn  mode   a  b  c  d  r  o  bus    a  b  c  d  bus
0b1010000000000000  0b011  1  0  0  0  0  0  0      1  0  0  0  0
0b1010000100000000  0b011  0  1  0  0  0  0  0      1  0  0  0  0
0b1010001000000000  0b011  0  0  1  0  0  0  0      1  0  0  0  0
0b1010001100000000  0b011  0  0  0  1  0  0  0      1  0  0  0  0
0b1010100000000000  0b011  0  0  0  0  1  0  0      1  0  0  0  0
0b1010100100000000  0b011  0  0  0  0  0  1  0      1  0  0  0  0

0b1010000100100000  0b011  0  1  0  0  0  0  0      0  1  0  0  0
0b1010001001000000  0b011  0  0  1  0  0  0  0      0  0  1  0  0
0b1010001101100000  0b011  0  0  0  1  0  0  0      0  0  0  1  0
*/

/* Test case bus tests:
instruction  mode  bus_address  read_a  read_b  read_c  read_d  read_bus  write_a  write_b  write_c  write_d  write_bus
# 1011maaavvv_____
0b1011000000000000  0b011  0b000  0  0  0  0  1    1  0  0  0  0
0b1011000000100000  0b011  0b000  0  0  0  0  1    0  1  0  0  0
0b1011000001000000  0b011  0b000  0  0  0  0  1    0  0  1  0  0
0b1011000001100000  0b011  0b000  0  0  0  0  1    0  0  0  1  0

0b1011100000000000  0b011  0b000  1  0  0  0  0    0  0  0  0  1
0b1011100000100000  0b011  0b000  0  1  0  0  0    0  0  0  0  1
0b1011100001000000  0b011  0b000  0  0  1  0  0    0  0  0  0  1
0b1011100001100000  0b011  0b000  0  0  0  1  0    0  0  0  0  1

0b1011000100000000  0b011  0b001  0  0  0  0  1    1  0  0  0  0
0b1011001000100000  0b011  0b010  0  0  0  0  1    0  1  0  0  0
0b1011001101000000  0b011  0b011  0  0  0  0  1    0  0  1  0  0
0b1011010001100000  0b011  0b100  0  0  0  0  1    0  0  0  1  0

0b1011100100000000  0b011  0b001  1  0  0  0  0    0  0  0  0  1
0b1011101000100000  0b011  0b010  0  1  0  0  0    0  0  0  0  1
0b1011101101000000  0b011  0b011  0  0  1  0  0    0  0  0  0  1
0b1011110001100000  0b011  0b100  0  0  0  1  0    0  0  0  0  1
*/

/* Test case misc tests:
instruction mode
0b1110000000000000  0b100
0b1110000000000001  0b101
*/
