// Digital circuit decoder.dig as structural Verilog
// modes:
// 	000
// 	001 alu
// 	010 jump
// 	011 read/write
// 	100 noop
// 	101 break
// 	110
// 	111
// 	at all times, use addr_sel for the bus address output.
// 	in alu mode, use X_sel, Y_sel, and OP, and write ALU output to Z_sel if possible.
// 	in jump mode, use X_sel, Y_sel, and the 3 least significant bits of OP, and write Z_sel to PC if comparison succeeds.
// 	in read/write mode, write X_sel to Z_sel.
// 	in noop mode, do not write to any destination.
// 	in break mode, do not write to any destination and set the BRK pin high.
// selections:
// 	0000 A register
// 	0001 B register
// 	0010 C register
// 	0011 D register
// 	1000 remainder register
// 	1001 flags register
// 	1101 constant
// 	1110 ALU output
// 	1111 bus input
module decoder (
  input  [15:0] instruction,
  output [15:0] constant,
  output [3:0] Y_sel,
  output [3:0] X_sel,
  output [3:0] Z_sel,
  output [2:0] mode,
  output [4:0] OP,
  output [3:0] addr_sel
);

  wire demultiplexer_2_out_1, enable_alu, enable_bus, enable_constant, enable_jump, enable_misc, enable_mov,
       not_1_out;
  wire [2:0] multiplexer_1_out;
  wire [3:0] multiplexer_2_out, multiplexer_3_out;

  Demultiplexer demultiplexer_1 (.sel(instruction[14]), .in(not_1_out), .out_0(enable_constant), .out_1(enable_alu));
  not not_1 (not_1_out, instruction[15]);
  Demultiplexer #(.Selector_Bits(2)) demultiplexer_2 (
    .sel(instruction[14:13]), .in(instruction[15]), .out_0(enable_jump), .out_1(demultiplexer_2_out_1),
    .out_3(enable_misc));  // open: out_2
  assign constant[11:0] = enable_constant ? instruction[11:0] : 12'bz;  // Driver driver_1
  Multiplexer #(.Bits(3)) multiplexer_1 (.sel(instruction[0]), .in_0(3'b100), .in_1(3'b101), .out(multiplexer_1_out));
  assign mode = enable_misc ? multiplexer_1_out : 3'bz;  // Driver driver_2
  assign X_sel = enable_mov ? instruction[11:8] : 4'bz;  // Driver driver_3
  assign Z_sel = enable_mov ? {1'b0, instruction[7:5]} : 4'bz;  // Driver driver_4
  assign mode = enable_constant ? 3'b011 : 3'bz;  // Driver driver_5
  assign mode = enable_alu ? 3'b001 : 3'bz;  // Driver driver_6
  assign mode = enable_jump ? 3'b010 : 3'bz;  // Driver driver_7
  assign Z_sel = enable_constant ? {2'b00, instruction[13:12]} : 4'bz;  // Driver driver_8
  assign X_sel = enable_constant ? 4'b1101 : 4'bz;  // Driver driver_9
  Multiplexer #(.Bits(4)) multiplexer_2 (
    .sel(instruction[11]), .in_0({1'b0, instruction[7:5]}), .in_1(4'b1111), .out(multiplexer_2_out));
  Multiplexer #(.Bits(4)) multiplexer_3 (
    .sel(instruction[11]), .in_0(4'b1111), .in_1({1'b0, instruction[7:5]}), .out(multiplexer_3_out));
  assign X_sel = enable_alu ? {2'b00, instruction[13:12]} : 4'bz;  // Driver driver_10
  assign Y_sel = enable_alu ? {2'b00, instruction[11:10]} : 4'bz;  // Driver driver_11
  assign Z_sel = enable_alu ? {2'b00, instruction[9:8]} : 4'bz;  // Driver driver_12
  assign OP = enable_alu ? instruction[7:3] : 5'bz;  // Driver driver_13
  assign X_sel = enable_jump ? {2'b00, instruction[12:11]} : 4'bz;  // Driver driver_14
  assign Y_sel = enable_jump ? {2'b00, instruction[10:9]} : 4'bz;  // Driver driver_15
  assign Z_sel = enable_jump ? {2'b00, instruction[8:7]} : 4'bz;  // Driver driver_16
  assign OP = enable_jump ? {2'b00, instruction[6:4]} : 5'bz;  // Driver driver_17
  assign addr_sel = enable_bus ? {1'b0, instruction[10:8]} : 4'bz;  // Driver driver_18
  assign Z_sel = enable_bus ? multiplexer_2_out : 4'bz;  // Driver driver_19
  assign X_sel = enable_bus ? multiplexer_3_out : 4'bz;  // Driver driver_20
  Demultiplexer demultiplexer_3 (
    .sel(instruction[12]), .in(demultiplexer_2_out_1), .out_0(enable_mov), .out_1(enable_bus));
  assign mode = enable_mov ? 3'b011 : 3'bz;  // Driver driver_21
  assign mode = enable_bus ? 3'b011 : 3'bz;  // Driver driver_22
  // Probe enable_constant on enable_constant
  // Probe enable_alu on enable_alu
  // Probe enable_jump on enable_jump
  // Probe enable_mov on enable_mov
  // Probe enable_bus on enable_bus
  // Probe enable_misc on enable_misc

  assign constant[15:12] = 4'b0000;

  // Other names for the same wires on the sheet: constant_value[11:0] = constant[11:0]; bus_address[3:0] = addr_sel

  // Notes on the sheet:
  //   mode
  //   constant
  //   alu
  //   jump
  //   mov
  //   bus
  //   misc
  //   output
  //   modes:
  //   	000
  //   	001 alu
  //   	010 jump
  //   	011 read/write
  //   	100 noop
  //   	101 break
  //   	110
  //   	111
  //   	at all times, use addr_sel for the bus address output.
  //   	in alu mode, use X_sel, Y_sel, and OP, and write ALU output to Z_sel if possible.
  //   	in jump mode, use X_sel, Y_sel, and the 3 least significant bits of OP, and write Z_sel to PC if comparison succeeds.
  //   	in read/write mode, write X_sel to Z_sel.
  //   	in noop mode, do not write to any destination.
  //   	in break mode, do not write to any destination and set the BRK pin high.
  //   selections:
  //   	0000 A register
  //   	0001 B register
  //   	0010 C register
  //   	0011 D register
  //   	1000 remainder register
  //   	1001 flags register
  //   	1101 constant
  //   	1110 ALU output
  //   	1111 bus input
endmodule

/* Test case mode tests:
instruction  mode  enable_constant  enable_alu  enable_jump  enable_mov  enable_bus  enable_misc
# ldc
0b0000000000000000  0b011  1  0  0  0  0  0
# alu
0b0100000000000000  0b001  0  1  0  0  0  0

# jump
0b1000000000000000  0b010  0  0  1  0  0  0

# mov
0b1010000000000000  0b011  0  0  0  1  0  0

# bus
0b1011000000000000  0b011  0  0  0  0  1  0

# misc (todo)
#0b1110000000000000  0b100  0  0  0  0  0  1
*/

/* Test case ldc tests:
instruction         mode   X_sel   Y_sel   Z_sel   constant
# 00rrvvvvvvvvvvvv
0b0000000000000000  0b011  0b1101  x       0b0000  0b000000000000
0b0001000000000000  0b011  0b1101  x       0b0001  0b000000000000
0b0010000000000000  0b011  0b1101  x       0b0010  0b000000000000
0b0011000000000000  0b011  0b1101  x       0b0011  0b000000000000

0b0000101010000001  0b011  0b1101  x       0b0000  0b101010000001
0b0001101010000001  0b011  0b1101  x       0b0001  0b101010000001
0b0010101010000001  0b011  0b1101  x       0b0010  0b101010000001
0b0011101010000001  0b011  0b1101  x       0b0011  0b101010000001
*/

/* Test case alu tests:
instruction         mode   X_sel   Y_sel   Z_sel   OP
# 01xxyywwooooonnn
0b0100000000000000  0b001  0b0000  0b0000  0b0000  0b00000
0b0100000100000000  0b001  0b0000  0b0000  0b0001  0b00000
0b0100001000000000  0b001  0b0000  0b0000  0b0010  0b00000
0b0100001100000000  0b001  0b0000  0b0000  0b0011  0b00000

0b0100010000000000  0b001  0b0000  0b0001  0b0000  0b00000
0b0100100100000000  0b001  0b0000  0b0010  0b0001  0b00000
0b0101001000000000  0b001  0b0001  0b0000  0b0010  0b00000
0b0110001100000000  0b001  0b0010  0b0000  0b0011  0b00000

0b0100010010000000  0b001  0b0000  0b0001  0b0000  0b10000
0b0100100100100000  0b001  0b0000  0b0010  0b0001  0b00100
0b0101001000110000  0b001  0b0001  0b0000  0b0010  0b00110
0b0110001100001000  0b001  0b0010  0b0000  0b0011  0b00001
*/

/* Test case jump tests:
instruction         mode   X_sel   Y_sel   Z_sel   OP
# 100xxyyttcccnnnn
0b1000000000000000  0b010  0b0000  0b0000  0b0000  0b00000

0b1001000000000000  0b010  0b0010  0b0000  0b0000  0b00000
0b1000100000000000  0b010  0b0001  0b0000  0b0000  0b00000
0b1000010000000000  0b010  0b0000  0b0010  0b0000  0b00000
0b1000001000000000  0b010  0b0000  0b0001  0b0000  0b00000

0b1001000000000000  0b010  0b0010  0b0000  0b0000  0b00000
0b1001100000000000  0b010  0b0011  0b0000  0b0000  0b00000
0b1000011000000000  0b010  0b0000  0b0011  0b0000  0b00000
0b1000001000000000  0b010  0b0000  0b0001  0b0000  0b00000

0b1001000100000000  0b010  0b0010  0b0000  0b0010  0b00000
0b1001100010000000  0b010  0b0011  0b0000  0b0001  0b00000
0b1000011110000000  0b010  0b0000  0b0011  0b0011  0b00000
0b1000001000000000  0b010  0b0000  0b0001  0b0000  0b00000

0b1001000101000000  0b010  0b0010  0b0000  0b0010  0b00100
0b1001100010100000  0b010  0b0011  0b0000  0b0001  0b00010
0b1000011110010000  0b010  0b0000  0b0011  0b0011  0b00001
0b1000001000110000  0b010  0b0000  0b0001  0b0000  0b00011
0b1000001001100000  0b010  0b0000  0b0001  0b0000  0b00110
0b1000001001110000  0b010  0b0000  0b0001  0b0000  0b00111
*/

/* Test case mov tests:
instruction         mode   X_sel   Y_sel   Z_sel
# 1010sssstttnnnnn  mode   a  b  c  d  r  o  bus    a  b  c  d  bus
0b1010000000000000  0b011  1  0  0  0  0  0  0      1  0  0  0  0     
0b1010000100000000  0b011  0  1  0  0  0  0  0      1  0  0  0  0
0b1010001000000000  0b011  0  0  1  0  0  0  0      1  0  0  0  0
0b1010001100000000  0b011  0  0  0  1  0  0  0      1  0  0  0  0
0b1010100000000000  0b011  0  0  0  0  1  0  0      1  0  0  0  0
0b1010100100000000  0b011  0  0  0  0  0  1  0      1  0  0  0  0

0b1010000100100000  0b011  0  1  0  0  0  0  0      0  1  0  0  0
0b1010001001000000  0b011  0  0  1  0  0  0  0      0  0  1  0  0
0b1010001101100000  0b011  0  0  0  1  0  0  0      0  0  0  1  0
*/

/* Test case bus tests:
instruction  mode  bus_address  read_a  read_b  read_c  read_d  read_bus  write_a  write_b  write_c  write_d  write_bus
# 1011maaavvv_____
0b1011000000000000  0b011  0b000  0  0  0  0  1    1  0  0  0  0
0b1011000000100000  0b011  0b000  0  0  0  0  1    0  1  0  0  0
0b1011000001000000  0b011  0b000  0  0  0  0  1    0  0  1  0  0
0b1011000001100000  0b011  0b000  0  0  0  0  1    0  0  0  1  0

0b1011100000000000  0b011  0b000  1  0  0  0  0    0  0  0  0  1
0b1011100000100000  0b011  0b000  0  1  0  0  0    0  0  0  0  1
0b1011100001000000  0b011  0b000  0  0  1  0  0    0  0  0  0  1
0b1011100001100000  0b011  0b000  0  0  0  1  0    0  0  0  0  1

0b1011000100000000  0b011  0b001  0  0  0  0  1    1  0  0  0  0
0b1011001000100000  0b011  0b010  0  0  0  0  1    0  1  0  0  0
0b1011001101000000  0b011  0b011  0  0  0  0  1    0  0  1  0  0
0b1011010001100000  0b011  0b100  0  0  0  0  1    0  0  0  1  0

0b1011100100000000  0b011  0b001  1  0  0  0  0    0  0  0  0  1
0b1011101000100000  0b011  0b010  0  1  0  0  0    0  0  0  0  1
0b1011101101000000  0b011  0b011  0  0  1  0  0    0  0  0  0  1
0b1011110001100000  0b011  0b100  0  0  0  1  0    0  0  0  0  1
*/

/* Test case misc tests:
instruction mode
0b1110000000000000  0b100
0b1110000000000001  0b101
*/
