// Digital circuit operand_selector.dig as structural Verilog
module operand_selector (
  input  [15:0] reg_A,
  input  [15:0] reg_B,
  input  [15:0] reg_C,
  input  [15:0] reg_D,
  input  [15:0] reg_rem,
  input  [15:0] reg_flags,
  input  [15:0] jump,
  input  [15:0] PC,
  input  [15:0] ALU,
  input  [15:0] bus,
  input  [15:0] constant,
  input  [3:0] X_sel,
  input  [3:0] Y_sel,
  input  [3:0] Z_sel,
  input  [3:0] D_sel,
  input  [3:0] addr_sel,
  output [15:0] X,
  output [15:0] Y,
  output [15:0] D,
  output [15:0] Z,
  output [15:0] addr
);

  value_selector u_X (
    .reg_A(reg_A), .reg_B(reg_B), .reg_C(reg_C), .reg_D(reg_D), .reg_rem(reg_rem), .reg_flags(reg_flags),
    .jump(jump), .PC(PC), .ALU(ALU), .bus(bus), .constant(constant), .sel(X_sel), .val(X));
  value_selector u_Z (
    .reg_A(reg_A), .reg_B(reg_B), .reg_C(reg_C), .reg_D(reg_D), .reg_rem(reg_rem), .reg_flags(reg_flags),
    .jump(jump), .PC(PC), .ALU(ALU), .bus(bus), .constant(constant), .sel(Z_sel), .val(Z));
  value_selector u_addr (
    .reg_A(reg_A), .reg_B(reg_B), .reg_C(reg_C), .reg_D(reg_D), .reg_rem(reg_rem), .reg_flags(reg_flags),
    .jump(jump), .PC(PC), .ALU(ALU), .bus(bus), .constant(constant), .sel(addr_sel), .val(addr));
  value_selector u_Y (
    .reg_A(reg_A), .reg_B(reg_B), .reg_C(reg_C), .reg_D(reg_D), .reg_rem(reg_rem), .reg_flags(reg_flags),
    .jump(jump), .PC(PC), .ALU(ALU), .bus(bus), .constant(constant), .sel(Y_sel), .val(Y));
  value_selector u_D (
    .reg_A(reg_A), .reg_B(reg_B), .reg_C(reg_C), .reg_D(reg_D), .reg_rem(reg_rem), .reg_flags(reg_flags),
    .jump(jump), .PC(PC), .ALU(ALU), .bus(bus), .constant(constant), .sel(D_sel), .val(D));
endmodule
