// Digital circuit value_selector.dig as structural Verilog
module value_selector (
  input  [15:0] reg_A,
  input  [15:0] reg_B,
  input  [15:0] reg_C,
  input  [15:0] reg_D,
  input  [15:0] reg_rem,
  input  [15:0] reg_flags,
  input  [15:0] jump,
  input  [15:0] PC,
  input  [15:0] ALU,
  input  [15:0] bus,
  input  [15:0] constant,
  input  [3:0] sel,
  output [15:0] val
);

  wire [15:1] undriven;

  Multiplexer #(.Selector_Bits(4), .Bits(16)) multiplexer_1 (
    .sel(sel), .in_0(reg_A), .in_1(reg_B), .in_2(reg_C), .in_3(reg_D), .in_4({16{1'b0}}), .in_5({16{1'b0}}),
    .in_6({16{1'b0}}), .in_7({16{1'b0}}), .in_8(reg_rem), .in_9(reg_flags), .in_10(jump), .in_11(PC),
    .in_12({undriven, 1'b0}), .in_13(constant), .in_14(ALU), .in_15(bus), .out(val));
  // Pins of 1 and 16 bits meet at {undriven, 1'b0}
endmodule
