// Digital circuit decoder.dig as structural Verilog
module decoder (
  input  [15:0] instruction,
  output [2:0] mode,
  output [15:0] arg0,
  output [15:0] arg1,
  output [15:0] arg2,
  output [15:0] arg3
);

  wire and_1_out, and_2_out, and_3_out, and_4_out, and_5_out, not_1_out, not_2_out;
  wire [2:0] priorityencoder_1_num;
  wire [7:0] bus_arg2;

  and and_1 (and_1_out, instruction[10], ~instruction[11]);  // And
  and and_2 (and_2_out, ~instruction[10], ~instruction[11]);  // And
  and and_3 (and_3_out, ~instruction[12], instruction[13]);  // And
  and and_4 (and_4_out, instruction[12], ~instruction[13]);  // And
  and and_5 (and_5_out, ~instruction[12], ~instruction[13]);  // And
  not not_1 (not_1_out, instruction[14]);
  not not_2 (not_2_out, instruction[15]);
  PriorityEncoder #(.Selector_Bits(3)) priorityencoder_1 (
    .in0(1'b1), .in1(and_1_out), .in2(and_2_out), .in3(and_3_out), .in4(and_4_out), .in5(and_5_out),
    .in6(not_1_out), .in7(not_2_out), .num(priorityencoder_1_num));  // open: any
  Multiplexer #(.Bits(8)) multiplexer_1 (
    .sel(instruction[11]), .in_0({{5{1'b0}}, instruction[2:0]}), .in_1(instruction[7:0]), .out(bus_arg2));
  assign mode = ~priorityencoder_1_num;  // Not not_3, 3 bits wide
  Multiplexer #(.Selector_Bits(3), .Bits(16)) multiplexer_2 (
    .sel(mode), .in_0({{13{1'b0}}, instruction[14:12]}), .in_1({{13{1'b0}}, instruction[13:11]}),
    .in_2({{13{1'b0}}, instruction[11:9]}), .in_3({{15{1'b0}}, instruction[11]}),
    .in_4({{14{1'b0}}, instruction[11:10]}), .in_5({{15{1'b0}}, instruction[9]}),
    .in_6({{13{1'b0}}, instruction[9:7]}), .in_7({16{1'b0}}), .out(arg0));
  Multiplexer #(.Selector_Bits(3), .Bits(16)) multiplexer_3 (
    .sel(mode), .in_0({4'b0000, instruction[11:0]}), .in_1({{13{1'b0}}, instruction[10:8]}),
    .in_2({{7{1'b0}}, instruction[8:0]}), .in_3({{13{1'b0}}, instruction[10:8]}),
    .in_4({{13{1'b0}}, instruction[9:7]}), .in_5({{7{1'b0}}, instruction[8:0]}),
    .in_6({{12{1'b0}}, instruction[3:0]}), .in_7({16{1'b0}}), .out(arg1));
  Multiplexer #(.Selector_Bits(3), .Bits(16)) multiplexer_4 (
    .sel(mode), .in_0({16{1'b0}}), .in_1({{12{1'b0}}, instruction[7:4]}), .in_2({16{1'b0}}),
    .in_3({{8{1'b0}}, bus_arg2}), .in_4({{9{1'b0}}, instruction[6:0]}), .in_5({16{1'b0}}), .in_6({16{1'b0}}),
    .in_7({16{1'b0}}), .out(arg2));
  Multiplexer #(.Selector_Bits(3), .Bits(16)) multiplexer_5 (
    .sel(mode), .in_0({16{1'b0}}), .in_1({{12{1'b0}}, instruction[3:0]}), .in_2({16{1'b0}}),
    .in_3({16{1'b0}}), .in_4({16{1'b0}}), .in_5({16{1'b0}}), .in_6({16{1'b0}}), .in_7({16{1'b0}}), .out(arg3));

  // Other names for the same wires on the sheet: alu_arg3[3:0] = instruction[3:0]; brk_arg1[8:0] = instruction[8:0];
  //   jump_arg2[6:0] = instruction[6:0]; ldc_arg1[11:0] = instruction[11:0]; lde_arg1[3:0] = instruction[3:0];
  //   mov_arg1[8:0] = instruction[8:0]; alu_arg2[3:0] = instruction[7:4]; jump_arg1[2:0] = instruction[9:7];
  //   lde_arg0[2:0] = instruction[9:7]; alu_arg1[2:0] = instruction[10:8]; bus_arg1[2:0] = instruction[10:8];
  //   brk_arg0[0] = instruction[9]; mov_arg0[2:0] = instruction[11:9]; jump_arg0[1:0] = instruction[11:10];
  //   alu_arg0[2:0] = instruction[13:11]; bus_arg0[0] = instruction[11]; ldc_arg0[2:0] = instruction[14:12]

  // Notes on the sheet:
  //   ldc
  //   alu
  //   mov
  //   bus
  //   jump
  //   noop/break
  //   lde
  //   ldc:
  //   arg0: write register
  //   arg1: constant unsigned 14
  //   alu
  //   arg0: write register
  //   arg1: lhs register
  //   arg2: rhs 4-bit
  //   arg3: opcode
  //   mov
  //   arg0: write register
  //   arg1: read register 9
  //   bus:
  //   arg0: load (0) store (1)
  //   arg1: address register
  //   arg2: value 8-bit
  //   jump:
  //   arg0: condition (see doc)
  //   arg1: comparand register
  //   arg2: jump target 7-bit
  //   noop/break
  //   arg0: brk pin value 1
  //   arg1: address 9-bit
  //   lde:
  //   arg0: write register
  //   arg1: constant unsigned 4
  //   mode:
  //   000: ldc
  //   001: alu
  //   010: mov
  //   011: bus
  //   100: jump
  //   101: noop/break
  //   110: lde
  //   111: unassigned
endmodule

/* Test case mode tests:
instruction         mode
# ldc
0b0000000000000000  0b000
0b0100000000000000  0b000
0b0110000000000000  0b000

# alu
0b1000000000000000  0b001
0b1010000000000000  0b001

# mov
0b1100000000000000  0b010
0b1100100000000000  0b010

# bus
0b1101000000000000  0b011
0b1101100000000000  0b011

# jump
0b1110000000000000  0b100
0b1110100000000000  0b100

# noop/break
0b1111000000000000  0b101
0b1111001000000000  0b101

# lde
0b1111010000000000  0b110
0b1111011000000000  0b110

# unassigned
0b1111100000000000  0b111
0b1111101000000000  0b111
0b1111110000000000  0b111
0b1111111000000000  0b111
*/

/* Test case ldc test cases:
instruction         mode   arg0  arg1
0b0100000000000000  0b000  0b100  0x00
0b0010000000000000  0b000  0b010  0x00
0b0111000000000000  0b000  0b111  0x00
0b0110000000000000  0b000  0b110  0x00

0b0110000000000001  0b000  0b110  0x01
0b0110000000000010  0b000  0b110  0x02
0b0110000000000100  0b000  0b110  0x04
0b0110000000001000  0b000  0b110  0x08
0b0110111111111111  0b000  0b110  0x0FFF
*/

/* Test case alu test cases:
instruction         mode   arg0  arg1  arg2  arg3
#b10wwwlllrrrroooo
0b1000101001001010  0b001  0b001 0b010 0b0100 0b1010
0b1011100011110000  0b001  0b111 0b000 0b1111 0b0000
*/

/* Test case mov test cases:
instruction         mode   arg0  arg1
#b1100wwwrrrrrrrrr
0b1100001000000101  0b010  0b001 0b000000101
0b1100111001010100  0b010  0b111 0b001010100
*/

/* Test case bus test cases:
instruction         mode   arg0 arg1  arg2
#b11010aaaZZZZZvvv
0b1101000101001010  0b011  0b0  0b001 0b010
0b1101011010110101  0b011  0b0  0b110 0b101


#b11011aaavvvvvvvv
0b1101100101001010  0b011  0b1  0b001 0b01001010
0b1101111010110101  0b011  0b1  0b110 0b10110101
*/

/* Test case jump test cases:
instruction         mode   arg0 arg1  arg2
#b1110ccCCCttttttt
0b1110011011001001  0b100  0b01 0b101 0b1001001
0b1110100100110110  0b100  0b10 0b010 0b0110110
*/

/* Test case brk test cases:
instruction         mode  arg0  arg1
#b111100Baaaaaaaaa
0b1111000110011001  0b101 0b0   0b110011001
0b1111001001100110  0b101 0b1   0b001100110
*/

/* Test case lde test cases:
instruction         mode   arg0  arg1
#b111101rrrZZvvvv
0b1111010101101100   0b110  0b010 0b1100
0b1111011011100011   0b110  0b101 0b0011
0b1111010100111100   0b110  0b010 0b1100
0b1111011010110011   0b110  0b101 0b0011
*/
