// Digital circuit nbit.dig as structural Verilog
module nbit (
  input  [15:0] value_in,
  input  [15:0] reg_in,
  input  enable,
  output [15:0] value_out,
  output [2:0] reg_ptr
);

  wire [3:3] undriven;

  Multiplexer #(.Bits(16), .generic("this.Bits = args.ValueSize;")) multiplexer_1 (
    .sel(value_in[3]), .in_0({{13{1'b0}}, value_in[2:0]}), .in_1(reg_in), .out(value_out));
  assign reg_ptr = enable ? value_in[2:0] : 3'bz;  // Driver driver_1
  // Pins of 3 and 4 bits meet at {undriven[3], value_in[2:0]}
endmodule

/* Test case 4-bit, 3 bit registers:
value_in  enable  reg_in  reg_ptr  value_out
0b0000    1       Z       x        0b000
0b0001    1       Z       x        0b001
0b0001    1       Z       x        0b001
0b0111    1       Z       x        0b111

0b1000    1       0x1245  0b000    0x1245
0b1001    1       0xABCD  0b001    0xABCD
0b1110    1       0xF0C5  0b110    0xF0C5



0b0000    0       Z       Z        x
0b0001    0       Z       Z        x
0b0001    0       Z       Z        x
0b0111    0       Z       Z        x

0b1000    0       0x1245  Z        x
0b1001    0       0xABCD  Z        x
0b1110    0       0xF0C5  Z        x
*/

/* Test case 5-bit, 3 bit registers:
value_in  enable  reg_in  reg_ptr  value_out
0b00000   1       Z       x        0b0000
0b00001   1       Z       x        0b0001
0b00001   1       Z       x        0b0001
0b01111   1       Z       x        0b1111

0b10000   1       0x1245  0b000    0x1245
0b10001   1       0xABCD  0b001    0xABCD
0b10110   1       0xF0C5  0b110    0xF0C5
0b11110   1       0xF0C5  0b110    0xF0C5



0b00000   0       Z       x        x
0b00001   0       Z       x        x
0b00001   0       Z       x        x
0b01111   0       Z       x        x

0b10000   0       0x1245  Z        x
0b10001   0       0xABCD  Z        x
0b10110   0       0xF0C5  Z        x
0b11110   0       0xF0C5  Z        x
*/

/* Test case 5-bit, 4 bit registers:
value_in   enable  reg_in  reg_ptr  value_out
0b00000    1       Z       x        0b0000
0b00001    1       Z       x        0b0001
0b00001    1       Z       x        0b0001
0b01111    1       Z       x        0b1111

0b10000    1       0x1245  0b0000   0x1245
0b10001    1       0xABCD  0b0001   0xABCD
0b11110    1       0xF0C5  0b1110   0xF0C5



0b00000    0       Z       x        x
0b00001    0       Z       x        x
0b00001    0       Z       x        x
0b01111    0       Z       x        x

0b10000    0       0x1245  Z        x
0b10001    0       0xABCD  Z        x
0b11110    0       0xF0C5  Z        x
*/

/* Code that sets the parameters or builds the circuit:
Bits := 4;
RegPtrSize := 3;
ValueSize := 16;
*/
