// Digital circuit proc16c1.dig as structural Verilog
module proc16c1 (
  input  [15:0] instruction_in,
  input  [15:0] data_in,
  input  clk,
  output [15:0] data_ptr,
  output [15:0] data_out,
  output data_write,
  output [15:0] instruction_ptr,
  output brk
);

  wire and_1_out, arg3, comparator_1_eq, enable_alu, enable_brk, enable_bus, enable_jump, enable_ldc,
       enable_lde, enable_mov, jump, multiplexer_2_out, nbit_1_value_out, not_1_out, reg_write;
  wire [2:0] mode, reg_ptr_a, reg_ptr_b, reg_ptr_write;
  wire [15:0] add_1_s, alu_1_p4, arg0, arg1, arg2, barrelshifter_1_out, jump_target, multiplexer_1_out,
       nbit_2_value_out, PC_q, reg_a, reg_b, reg_data;

  assign data_write = enable_alu ? 1'b0 : 1'bz;  // Driver driver_1
  assign reg_ptr_a = enable_alu ? arg1[2:0] : 3'bz;  // Driver driver_2
  nbit #(.generic("Bits := 4; RegPtrSize := 3; ValueSize := 16;")) nbit_1 (
    .value_in(arg2), .reg_in(reg_b), .enable(enable_alu), .value_out(nbit_1_value_out), .reg_ptr(reg_ptr_b));
  assign reg_ptr_a = enable_bus ? arg1[2:0] : 3'bz;  // Driver driver_3
  assign data_ptr = enable_bus ? reg_a : 16'bz;  // Driver driver_4
  // decoder decoder_1: pin names not known; wires that end beside it: instruction_in, mode, arg0, arg1, arg2, arg3
  nbit #(.generic("Bits := 8; RegPtrSize := 3; ValueSize := 16;")) nbit_2 (
    .value_in(arg2), .reg_in(reg_b), .enable(enable_bus), .value_out(nbit_2_value_out), .reg_ptr(reg_ptr_b));
  // alu alu_1: pin names not known; wires that end beside it: reg_a, nbit_1_value_out, arg3, alu_1_p4
  and and_1 (and_1_out, arg0[0], arg2[0]);
  Decoder #(.Selector_Bits(3)) decoder_2 (
    .sel(mode), .out_0(enable_ldc), .out_1(enable_alu), .out_2(enable_mov), .out_3(enable_bus),
    .out_4(enable_jump), .out_5(enable_brk), .out_6(enable_lde));  // open: out_7
  assign reg_data = enable_alu ? alu_1_p4 : 16'bz;  // Driver driver_5
  assign reg_write = enable_alu ? 1'b1 : 1'bz;  // Driver driver_6
  assign reg_ptr_write = enable_alu ? arg0[2:0] : 3'bz;  // Driver driver_7
  Multiplexer #(.Bits(16)) multiplexer_1 (
    .sel(and_1_out), .in_0(data_in), .in_1(nbit_2_value_out), .out(multiplexer_1_out));
  assign reg_ptr_write = enable_bus ? arg0[2:0] : 3'bz;  // Driver driver_8
  assign data_out = enable_bus ? multiplexer_1_out : 16'bz;  // Driver driver_9
  assign data_write = enable_bus ? and_1_out : 1'bz;  // Driver driver_10
  assign reg_write = enable_bus ? and_1_out : 1'bz;  // Driver driver_11
  assign reg_ptr_a = enable_mov ? arg1[2:0] : 3'bz;  // Driver driver_12
  assign reg_data = enable_mov ? reg_a : 16'bz;  // Driver driver_13
  assign data_write = enable_ldc ? 1'b0 : 1'bz;  // Driver driver_14
  assign reg_ptr_write = enable_ldc ? arg0[2:0] : 3'bz;  // Driver driver_15
  assign reg_write = enable_ldc ? 1'b1 : 1'bz;  // Driver driver_16
  assign reg_data = enable_ldc ? arg1 : 16'bz;  // Driver driver_17
  assign reg_ptr_write = enable_mov ? arg0[2:0] : 3'bz;  // Driver driver_18
  assign reg_write = enable_mov ? 1'b1 : 1'bz;  // Driver driver_19
  assign data_write = enable_mov ? 1'b0 : 1'bz;  // Driver driver_20
  Comparator #(.Bits(16), .Signed("true")) comparator_1 (
    .a(reg_a), .b({16{1'b0}}), .eq(comparator_1_eq));  // open: gt, lt
  assign reg_ptr_a = enable_jump ? arg1[2:0] : 3'bz;  // Driver driver_21
  not not_1 (not_1_out, comparator_1_eq);
  nbit #(.generic("Bits := 4; RegPtrSize := 3; ValueSize := 16;")) nbit_3 (
    .value_in(arg2), .reg_in(reg_b), .enable(enable_jump), .value_out(jump_target), .reg_ptr(reg_ptr_b));
  assign data_write = enable_brk ? 1'b0 : 1'bz;  // Driver driver_22
  nbit #(.generic("Bits := 9; RegPtrSize := 3; ValueSize := 16;")) nbit_4 (
    .value_in(arg1), .reg_in(reg_a), .enable(enable_jump), .value_out(data_ptr), .reg_ptr(reg_ptr_a));
  RegisterFile #(.AddrBits(3), .Bits(16)) registerfile_1 (
    .Din(reg_data), .we(reg_write), .Rw(reg_ptr_write), .C(clk), .Ra(reg_ptr_a), .Rb(reg_ptr_b), .Da(reg_a),
    .Db(reg_b));
  Multiplexer #(.Selector_Bits(2)) multiplexer_2 (
    .sel(arg0[1:0]), .in_0(1'b1), .in_1(comparator_1_eq), .in_2(not_1_out), .in_3(1'b0),
    .out(multiplexer_2_out));
  assign data_write = enable_jump ? 1'b0 : 1'bz;  // Driver driver_23
  and and_2 (jump, multiplexer_2_out, enable_jump);
  and and_3 (brk, enable_brk, arg0[0]);
  Register #(.Bits(16)) PC (.D(instruction_ptr), .C(clk), .en(1'b1), .Q(PC_q));
  BarrelShifter #(.Bits(16)) barrelshifter_1 (.in(reg_a), .shift(5'b00100), .out(barrelshifter_1_out));
  assign data_write = enable_lde ? 1'b0 : 1'bz;  // Driver driver_24
  assign reg_ptr_write = enable_lde ? arg0[2:0] : 3'bz;  // Driver driver_25
  Add #(.Bits(16)) add_1 (.a(PC_q), .b(16'h1), .c_i(1'b0), .s(add_1_s));  // open: c_o
  Multiplexer #(.Bits(16)) multiplexer_3 (.sel(jump), .in_0(add_1_s), .in_1(jump_target), .out(instruction_ptr));
  assign reg_data = barrelshifter_1_out | arg1;  // Or or_1, 16 bits wide
  assign reg_write = enable_lde ? 1'b1 : 1'bz;  // Driver driver_26
  assign reg_ptr_a = enable_lde ? arg0[2:0] : 3'bz;  // Driver driver_27

  // Other names for the same wires on the sheet: brk_out = brk; clock = clk

  // Notes on the sheet:
  //   input
  //   ↑ control elements                          ↓ instruction circuits
  //   alu
  //   alu
  //   arg0: write register
  //   arg1: lhs register
  //   arg2: rhs 4-bit
  //   arg3: opcode
  //   bus
  //   bus:
  //   arg0: load (0) store (1)
  //   arg1: address register
  //   arg2: value 8-bit
  //   output
  //   ldc
  //   ldc:
  //   arg0: write register
  //   arg1: unsigned constant
  //   mov
  //   mov
  //   arg0: write register
  //   arg1: read register
  //   register file
  //   jump
  //   jump:
  //   arg0: condition (see doc)
  //   arg1: comparand register
  //   arg2: jump target 7-bit
  //   noop/break
  //   noop/break
  //   arg0: brk pin value 1
  //   arg1: address 9-bit
  //   program counter
  //   lde
  //   lde:
  //   arg0: register
  //   arg1: unsigned constant
endmodule
