// Digital circuit alu16_1.dig as structural Verilog
module alu16_1 (
  input  [13:0] opcode,
  input  [15:0] A,
  input  [15:0] B,
  output [15:0] R
);

  wire comparator_1_eq, comparator_1_gt, comparator_1_lt, multiplexer_9_out, multiplexer_10_out,
       multiplexer_13_out, multiplexer_14_out, multiplexer_15_out, nor_1_out, not_3_out, not_4_out, not_5_out;
  wire [15:0] add_1_s, and_1_out, barrelshifter_1_out, barrelshifter_2_out, div_1_q, multiplexer_1_out,
       multiplexer_2_out, multiplexer_3_out, multiplexer_4_out, multiplexer_5_out, multiplexer_6_out,
       multiplexer_7_out, multiplexer_8_out, multiplexer_11_out, multiplexer_12_out, multiplexer_16_out,
       multiplexer_17_out, multiplexer_18_out, multiplexer_19_out, not_1_out, not_2_out, or_1_out, sub_1_s,
       xnor_1_out, xor_1_out;
  wire [31:0] mul_1_mul;

  Multiplexer #(.Selector_Bits(2), .Bits(16)) multiplexer_1 (
    .sel(opcode[13:12]), .in_0(A), .in_1({16{1'b0}}), .in_2(16'h1), .in_3({16{1'b1}}), .out(multiplexer_1_out));
  Multiplexer #(.Selector_Bits(2), .Bits(16)) multiplexer_2 (
    .sel(opcode[11:10]), .in_0(B), .in_1({16{1'b0}}), .in_2(16'h1), .in_3({16{1'b1}}), .out(multiplexer_2_out));
  Comparator #(.Bits(16), .Signed("true")) comparator_1 (
    .a(multiplexer_1_out), .b(multiplexer_2_out), .gt(comparator_1_gt), .eq(comparator_1_eq),
    .lt(comparator_1_lt));
  Add #(.Bits(16)) add_1 (.a(multiplexer_1_out), .b(multiplexer_2_out), .c_i(1'b0), .s(add_1_s));  // open: c_o
  Sub #(.Bits(16)) sub_1 (.a(multiplexer_1_out), .b(multiplexer_2_out), .c_i(1'b0), .s(sub_1_s));  // open: c_o
  Mul #(.Signed("true"), .Bits(16)) mul_1 (.a(multiplexer_1_out), .b(multiplexer_2_out), .mul(mul_1_mul));
  Div #(.Signed("true"), .Bits(16)) div_1 (.a(multiplexer_1_out), .b(multiplexer_2_out), .q(div_1_q));  // open: r
  BarrelShifter #(.Bits(16), .barrelSigned("true")) barrelshifter_1 (
    .in(multiplexer_1_out), .shift(multiplexer_2_out[5:0]), .out(barrelshifter_1_out));
  BarrelShifter #(.Bits(16), .barrelSigned("true"), .direction("right")) barrelshifter_2 (
    .in(multiplexer_1_out), .shift(multiplexer_2_out[5:0]), .out(barrelshifter_2_out));
  assign and_1_out = multiplexer_1_out & multiplexer_2_out;  // And and_1, 16 bits wide
  assign or_1_out = multiplexer_1_out | multiplexer_2_out;  // Or or_1, 16 bits wide
  assign not_1_out = ~multiplexer_1_out;  // Not not_1, 16 bits wide
  assign not_2_out = ~multiplexer_2_out;  // Not not_2, 16 bits wide
  assign xor_1_out = multiplexer_1_out ^ multiplexer_2_out;  // XOr xor_1, 16 bits wide
  assign xnor_1_out = ~(multiplexer_1_out ^ multiplexer_2_out);  // XNOr xnor_1, 16 bits wide
  not not_3 (not_3_out, comparator_1_lt);
  not not_4 (not_4_out, comparator_1_gt);
  nor nor_1 (nor_1_out, comparator_1_gt, comparator_1_lt);
  not not_5 (not_5_out, comparator_1_eq);
  Multiplexer #(.Bits(16)) multiplexer_3 (.sel(opcode[5]), .in_0(add_1_s), .in_1(sub_1_s), .out(multiplexer_3_out));
  Multiplexer #(.Bits(16)) multiplexer_4 (
    .sel(opcode[5]), .in_0(mul_1_mul[15:0]), .in_1(div_1_q), .out(multiplexer_4_out));
  Multiplexer #(.Bits(16)) multiplexer_5 (
    .sel(opcode[5]), .in_0(barrelshifter_1_out), .in_1(barrelshifter_2_out), .out(multiplexer_5_out));
  Multiplexer #(.Bits(16)) multiplexer_6 (.sel(opcode[5]), .in_0(and_1_out), .in_1(or_1_out), .out(multiplexer_6_out));
  Multiplexer #(.Bits(16)) multiplexer_7 (.sel(opcode[5]), .in_0(not_1_out), .in_1(not_2_out), .out(multiplexer_7_out));
  Multiplexer #(.Bits(16)) multiplexer_8 (
    .sel(opcode[5]), .in_0(xor_1_out), .in_1(xnor_1_out), .out(multiplexer_8_out));
  Multiplexer multiplexer_9 (.sel(opcode[5]), .in_0(comparator_1_gt), .in_1(comparator_1_lt), .out(multiplexer_9_out));
  Multiplexer multiplexer_10 (.sel(opcode[5]), .in_0(not_3_out), .in_1(not_4_out), .out(multiplexer_10_out));
  Multiplexer #(.Bits(16)) multiplexer_11 (
    .sel(opcode[6]), .in_0(multiplexer_3_out), .in_1(multiplexer_4_out), .out(multiplexer_11_out));
  Multiplexer #(.Bits(16)) multiplexer_12 (
    .sel(opcode[6]), .in_0(multiplexer_6_out), .in_1(multiplexer_7_out), .out(multiplexer_12_out));
  Multiplexer multiplexer_13 (
    .sel(opcode[6]), .in_0(multiplexer_9_out), .in_1(multiplexer_10_out), .out(multiplexer_13_out));
  Multiplexer multiplexer_14 (.sel(opcode[5]), .in_0(nor_1_out), .in_1(not_5_out), .out(multiplexer_14_out));
  Multiplexer multiplexer_15 (
    .sel(opcode[7]), .in_0(multiplexer_13_out), .in_1(multiplexer_14_out), .out(multiplexer_15_out));
  Multiplexer #(.Bits(16)) multiplexer_16 (
    .sel(opcode[7]), .in_0(multiplexer_11_out), .in_1(multiplexer_5_out), .out(multiplexer_16_out));
  Multiplexer #(.Bits(16)) multiplexer_17 (
    .sel(opcode[7]), .in_0(multiplexer_12_out), .in_1(multiplexer_8_out), .out(multiplexer_17_out));
  Multiplexer #(.Bits(16)) multiplexer_18 (
    .sel(multiplexer_15_out), .in_0({16{1'b0}}), .in_1({16{1'b1}}), .out(multiplexer_18_out));
  Multiplexer #(.Bits(16)) multiplexer_19 (
    .sel(opcode[8]), .in_0(multiplexer_17_out), .in_1(multiplexer_18_out), .out(multiplexer_19_out));
  Multiplexer #(.Bits(16)) multiplexer_20 (
    .sel(opcode[9]), .in_0(multiplexer_16_out), .in_1(multiplexer_19_out), .out(R));

  // Notes on the sheet:
  //   arithmetic
  //   logic
  //   comparison
endmodule

/* Test case arithmetic tests:
opcode           A       B       R
# addition
# XsYsAluop---AB
0b00000000000000  0x0000  0x0000  0x0000
0b00000000000000  0x0001  0x0000  0x0001
0b00000000000000  0x0000  0x0001  0x0001
0b00000000000000  0x0001  0x0001  0x0002
0b00000000000000  0x0002  0x0003  0x0005

# subtraction
# XsYsAluop---AB
0b00000000100000  0x0000  0x0000  0x0000
0b00000000100000  0x0001  0x0000  0x0001
0b00000000100000  0x0001  0x0001  0x0000
0b00000000100000  0x0002  0x0001  0x0001
0b00000000100000  0x0002  0x0000  0x0002
0b00000000100000  0x0001  0x0002  0xFFFF
0b00000000100000  0x0000  0x0001  0xFFFF
0b00000000100000  0x0000  0x0002  0xFFFE

# multiplication
# XsYsAluop---AB
0b00000001000000  0x0000  0x0000  0x0000
0b00000001000000  0x0001  0x0000  0x0000
0b00000001000000  0x0000  0x0001  0x0000
0b00000001000000  0x0001  0x0001  0x0001
0b00000001000000  0x0000  0x0002  0x0000
0b00000001000000  0x0002  0x0000  0x0000
0b00000001000000  0x0002  0x0002  0x0004
0b00000001000000  0x0002  0x0001  0x0002
0b00000001000000  0x0001  0x0002  0x0002
0b00000001000000  0xFFFF  0x0002  0xFFFE
0b00000001000000  0x0002  0xFFFF  0xFFFE

# division
# XsYsAluop---AB
0b00000001100000  0x0000  0x0000  X

0b00000001100000  0x0001  0x0001  1
0b00000001100000  0x0002  0x0001  2
0b00000001100000  0x0003  0x0001  3
0b00000001100000  0x0004  0x0001  4
0b00000001100000  0x0005  0x0001  5
0b00000001100000  0x0006  0x0001  6
0b00000001100000  0x0007  0x0001  7

0b00000001100000  0x0001  0x0002  0
0b00000001100000  0x0002  0x0002  1
0b00000001100000  0x0003  0x0002  1
0b00000001100000  0x0004  0x0002  2
0b00000001100000  0x0005  0x0002  2
0b00000001100000  0x0006  0x0002  3
0b00000001100000  0x0007  0x0002  3
*/

/* Test case bitwise tests:
opcode            A       B       R
# bitwise and
# XsYsAluop---AB
0b00001000000000  0x0000  0x0000  0x0000
0b00001000000000  0x0000  0x0001  0x0000
0b00001000000000  0x0001  0x0000  0x0000
0b00001000000000  0x0001  0x0001  0x0001
0b00001000000000  0x0002  0x0001  0x0000
0b00001000000000  0x0001  0x0002  0x0000
0b00001000000000  0x0002  0x0002  0x0002
0b00001000000000  0x0002  0x0000  0x0000
0b00001000000000  0x0000  0x0002  0x0000
0b00001000000000  0x0003  0x0002  0x0002

# bitwise or
# XsYsAluop---AB
0b00001000100000  0x0000  0x0000  0x0000
0b00001000100000  0x0000  0x0001  0x0001
0b00001000100000  0x0001  0x0000  0x0001
0b00001000100000  0x0001  0x0001  0x0001
0b00001000100000  0x0002  0x0001  0x0003
0b00001000100000  0x0001  0x0002  0x0003
0b00001000100000  0x0002  0x0002  0x0002
0b00001000100000  0x0002  0x0000  0x0002
0b00001000100000  0x0000  0x0002  0x0002
0b00001000100000  0x0003  0x0002  0x0003

# bitwise not x
# XsYsAluop---AB
0b00001001000000  0x0000  0x0000  0xFFFF
0b00001001000000  0x0000  0x0001  0xFFFF
0b00001001000000  0x0001  0x0000  0xFFFE
0b00001001000000  0x0001  0x0001  0xFFFE
0b00001001000000  0x0002  0x0000  0xFFFD
0b00001001000000  0x0002  0x0001  0xFFFD
0b00001001000000  0x0003  0x0000  0xFFFC
0b00001001000000  0x0003  0x0001  0xFFFC
0b00001001000000  0x0004  0x0000  0xFFFB
0b00001001000000  0x0004  0x0001  0xFFFB

# bitwise not y
# XsYsAluop---AB
0b00001001100000  0x0000  0x0000  0xFFFF
0b00001001100000  0x0001  0x0000  0xFFFF
0b00001001100000  0x0000  0x0001  0xFFFE
0b00001001100000  0x0001  0x0001  0xFFFE
0b00001001100000  0x0000  0x0002  0xFFFD
0b00001001100000  0x0001  0x0002  0xFFFD
0b00001001100000  0x0000  0x0003  0xFFFC
0b00001001100000  0x0001  0x0003  0xFFFC
0b00001001100000  0x0000  0x0004  0xFFFB
0b00001001100000  0x0001  0x0004  0xFFFB

# bitwise xor
# XsYsAluop---AB
0b00001010000000  0x0000  0x0000  0x0000
0b00001010000000  0x0001  0x0000  0x0001
0b00001010000000  0x0000  0x0001  0x0001
0b00001010000000  0x0001  0x0001  0x0000
0b00001010000000  0x0000  0x0002  0x0002
0b00001010000000  0x0001  0x0002  0x0003
0b00001010000000  0x0000  0x0003  0x0003
0b00001010000000  0x0001  0x0003  0x0002
0b00001010000000  0x0000  0x0004  0x0004

# bitwise xnor
# XsYsAluop---AB
0b00001010100000  0x0000  0x0000  0xFFFF
0b00001010100000  0x0001  0x0000  0xFFFE
0b00001010100000  0x0000  0x0001  0xFFFE
0b00001010100000  0x0001  0x0001  0xFFFF
0b00001010100000  0x0000  0x0002  0xFFFD
0b00001010100000  0x0001  0x0002  0xFFFC
0b00001010100000  0x0000  0x0003  0xFFFC
0b00001010100000  0x0001  0x0003  0xFFFD
0b00001010100000  0x0000  0x0004  0xFFFB
*/

/* Test case comparison tests:
opcode            A       B       R
# greater than
# XsYsAluop---AB
0b00001100000000  0x0000  0x0000  0x0000
0b00001100000000  0x0000  0x0001  0x0000
0b00001100000000  0x0001  0x0000  0xFFFF
0b00001100000000  0x0001  0x0001  0x0000
0b00001100000000  0x0002  0x0001  0xFFFF
0b00001100000000  0x0001  0x0002  0x0000
0b00001100000000  0x0002  0x0002  0x0000
0b00001100000000  0x0002  0x0000  0xFFFF
0b00001100000000  0x0000  0x0002  0x0000
0b00001100000000  0x0003  0x0002  0xFFFF

# less than
# XsYsAluop---AB
0b00001100100000  0x0000  0x0000  0x0000
0b00001100100000  0x0000  0x0001  0xFFFF
0b00001100100000  0x0001  0x0000  0x0000
0b00001100100000  0x0001  0x0001  0x0000
0b00001100100000  0x0002  0x0001  0x0000
0b00001100100000  0x0001  0x0002  0xFFFF
0b00001100100000  0x0002  0x0002  0x0000
0b00001100100000  0x0002  0x0000  0x0000
0b00001100100000  0x0000  0x0002  0xFFFF
0b00001100100000  0x0003  0x0002  0x0000

# greater than or equal
# XsYsAluop---AB
0b00001101000000  0x0000  0x0000  0xFFFF
0b00001101000000  0x0000  0x0001  0x0000
0b00001101000000  0x0001  0x0000  0xFFFF
0b00001101000000  0x0001  0x0001  0xFFFF
0b00001101000000  0x0002  0x0001  0xFFFF
0b00001101000000  0x0001  0x0002  0x0000
0b00001101000000  0x0002  0x0002  0xFFFF
0b00001101000000  0x0002  0x0000  0xFFFF
0b00001101000000  0x0000  0x0002  0x0000
0b00001101000000  0x0003  0x0002  0xFFFF

# less than or equal
# XsYsAluop---AB
0b00001101100000  0x0000  0x0000  0xFFFF
0b00001101100000  0x0000  0x0001  0xFFFF
0b00001101100000  0x0001  0x0000  0x0000
0b00001101100000  0x0001  0x0001  0xFFFF
0b00001101100000  0x0002  0x0001  0x0000
0b00001101100000  0x0001  0x0002  0xFFFF
0b00001101100000  0x0002  0x0002  0xFFFF
0b00001101100000  0x0002  0x0000  0x0000
0b00001101100000  0x0000  0x0002  0xFFFF
0b00001101100000  0x0003  0x0002  0x0000

# equal
# XsYsAluop---AB
0b00001110000000  0x0000  0x0000  0xFFFF
0b00001110000000  0x0000  0x0001  0x0000
0b00001110000000  0x0001  0x0000  0x0000
0b00001110000000  0x0001  0x0001  0xFFFF
0b00001110000000  0x0002  0x0001  0x0000
0b00001110000000  0x0001  0x0002  0x0000
0b00001110000000  0x0002  0x0002  0xFFFF
0b00001110000000  0x0002  0x0000  0x0000
0b00001110000000  0x0000  0x0002  0x0000
0b00001110000000  0x0003  0x0002  0x0000

# not equal
# XsYsAluop---AB
0b00001110100000  0x0000  0x0000  0x0000
0b00001110100000  0x0000  0x0001  0xFFFF
0b00001110100000  0x0001  0x0000  0xFFFF
0b00001110100000  0x0001  0x0001  0x0000
0b00001110100000  0x0002  0x0001  0xFFFF
0b00001110100000  0x0001  0x0002  0xFFFF
0b00001110100000  0x0002  0x0002  0x0000
0b00001110100000  0x0002  0x0000  0xFFFF
0b00001110100000  0x0000  0x0002  0xFFFF
0b00001110100000  0x0003  0x0002  0xFFFF
*/

/* Test case selection tests:
opcode            A       B       R
# select
# XsYsAluop---AB
0b00000000000000  0x0003  0x0005  0x0008
0b01000000000000  0x0003  0x0005  0x0005
0b10000000000000  0x0003  0x0005  0x0006
0b11000000000000  0x0003  0x0005  0x0004

0b00000000000000  0x0003  0x0005  0x0008
0b00010000000000  0x0003  0x0005  0x0003
0b00100000000000  0x0003  0x0005  0x0004
0b00110000000000  0x0003  0x0005  0x0002

0b01010000000000  0x0003  0x0005  0x0000
0b01100000000000  0x0003  0x0005  0x0001
0b01110000000000  0x0003  0x0005  0xFFFF

0b10010000000000  0x0003  0x0005  0x0001
0b10100000000000  0x0003  0x0005  0x0002
0b10110000000000  0x0003  0x0005  0x0000

0b11010000000000  0x0003  0x0005  0xFFFF
0b11100000000000  0x0003  0x0005  0x0000
0b11110000000000  0x0003  0x0005  0xFFFE
*/
