// Digital circuit alu16_2.dig as structural Verilog
module alu16_2 (
  input  [12:0] opcode,
  input  [15:0] A,
  input  [15:0] B,
  input  [15:0] Ax,
  output [15:0] R
);

  wire compare16_1_1_r;
  wire [15:0] add_1_s, and_1_out, barrelshifter_1_out, barrelshifter_2_out, div_1_q, multiplexer_1_out,
       multiplexer_2_out, multiplexer_3_out, multiplexer_4_out, multiplexer_5_out, multiplexer_6_out,
       multiplexer_7_out, multiplexer_8_out, multiplexer_9_out, multiplexer_10_out, multiplexer_11_out,
       multiplexer_12_out, multiplexer_13_out, multiplexer_14_out, multiplexer_15_out, multiplexer_16_out,
       multiplexer_17_out, multiplexer_18_out, nand_1_out, nor_1_out, not_1_out, not_2_out, or_1_out,
       sub_1_s, xnor_1_out, xor_1_out;
  wire [31:0] mul_1_mul;

  Multiplexer #(.Bits(16)) multiplexer_1 (.sel(opcode[12]), .in_0(A), .in_1(B), .out(multiplexer_1_out));
  Multiplexer #(.Bits(16)) multiplexer_2 (.sel(opcode[12]), .in_0(B), .in_1(A), .out(multiplexer_2_out));
  Multiplexer #(.Selector_Bits(2), .Bits(16)) multiplexer_3 (
    .sel(opcode[11:10]), .in_0(multiplexer_1_out), .in_1({16{1'b0}}), .in_2(16'h1), .in_3(Ax),
    .out(multiplexer_3_out));
  Multiplexer #(.Selector_Bits(2), .Bits(16)) multiplexer_4 (
    .sel(opcode[9:8]), .in_0(multiplexer_2_out), .in_1({16{1'b0}}), .in_2(16'h1), .in_3(Ax),
    .out(multiplexer_4_out));
  Add #(.Bits(16)) add_1 (.a(multiplexer_3_out), .b(multiplexer_4_out), .c_i(1'b0), .s(add_1_s));  // open: c_o
  Sub #(.Bits(16)) sub_1 (.a(multiplexer_3_out), .b(multiplexer_4_out), .c_i(1'b0), .s(sub_1_s));  // open: c_o
  Mul #(.Signed("true"), .Bits(16)) mul_1 (.a(multiplexer_3_out), .b(multiplexer_4_out), .mul(mul_1_mul));
  Div #(.Signed("true"), .Bits(16)) div_1 (.a(multiplexer_3_out), .b(multiplexer_4_out), .q(div_1_q));  // open: r
  BarrelShifter #(.Bits(16), .barrelSigned("true")) barrelshifter_1 (
    .in(multiplexer_3_out), .shift(multiplexer_4_out[5:0]), .out(barrelshifter_1_out));
  BarrelShifter #(.Bits(16), .barrelSigned("true"), .direction("right")) barrelshifter_2 (
    .in(multiplexer_3_out), .shift(multiplexer_4_out[5:0]), .out(barrelshifter_2_out));
  assign and_1_out = multiplexer_3_out & multiplexer_4_out;  // And and_1, 16 bits wide
  assign or_1_out = multiplexer_3_out | multiplexer_4_out;  // Or or_1, 16 bits wide
  assign not_1_out = ~multiplexer_3_out;  // Not not_1, 16 bits wide
  assign not_2_out = ~multiplexer_4_out;  // Not not_2, 16 bits wide
  assign xor_1_out = multiplexer_3_out ^ multiplexer_4_out;  // XOr xor_1, 16 bits wide
  assign xnor_1_out = ~(multiplexer_3_out ^ multiplexer_4_out);  // XNOr xnor_1, 16 bits wide
  assign nor_1_out = ~(multiplexer_3_out | multiplexer_4_out);  // NOr nor_1, 16 bits wide
  assign nand_1_out = ~(multiplexer_3_out & multiplexer_4_out);  // NAnd nand_1, 16 bits wide
  compare16_1 compare16_1_1 (.m(opcode[5:3]), .A(multiplexer_3_out), .B(multiplexer_4_out), .r(compare16_1_1_r));
  Multiplexer #(.Bits(16)) multiplexer_5 (.sel(opcode[3]), .in_0(add_1_s), .in_1(sub_1_s), .out(multiplexer_5_out));
  Multiplexer #(.Bits(16)) multiplexer_6 (
    .sel(opcode[3]), .in_0(mul_1_mul[15:0]), .in_1(div_1_q), .out(multiplexer_6_out));
  Multiplexer #(.Bits(16)) multiplexer_7 (
    .sel(opcode[3]), .in_0(barrelshifter_1_out), .in_1(barrelshifter_2_out), .out(multiplexer_7_out));
  Multiplexer #(.Bits(16)) multiplexer_8 (.sel(opcode[3]), .in_0(and_1_out), .in_1(or_1_out), .out(multiplexer_8_out));
  Multiplexer #(.Bits(16)) multiplexer_9 (.sel(opcode[3]), .in_0(not_1_out), .in_1(not_2_out), .out(multiplexer_9_out));
  Multiplexer #(.Bits(16)) multiplexer_10 (
    .sel(opcode[3]), .in_0(xor_1_out), .in_1(xnor_1_out), .out(multiplexer_10_out));
  Multiplexer #(.Bits(16)) multiplexer_11 (
    .sel(opcode[3]), .in_0(nor_1_out), .in_1(nand_1_out), .out(multiplexer_11_out));
  Multiplexer #(.Bits(16)) multiplexer_12 (
    .sel(opcode[4]), .in_0(multiplexer_5_out), .in_1(multiplexer_6_out), .out(multiplexer_12_out));
  Multiplexer #(.Bits(16)) multiplexer_13 (
    .sel(opcode[4]), .in_0(multiplexer_8_out), .in_1(multiplexer_9_out), .out(multiplexer_13_out));
  Multiplexer #(.Bits(16)) multiplexer_14 (
    .sel(opcode[4]), .in_0(multiplexer_10_out), .in_1(multiplexer_11_out), .out(multiplexer_14_out));
  Multiplexer #(.Bits(16)) multiplexer_15 (
    .sel(opcode[5]), .in_0(multiplexer_12_out), .in_1(multiplexer_7_out), .out(multiplexer_15_out));
  Multiplexer #(.Bits(16)) multiplexer_16 (
    .sel(opcode[5]), .in_0(multiplexer_13_out), .in_1(multiplexer_14_out), .out(multiplexer_16_out));
  Multiplexer #(.Bits(16)) multiplexer_17 (
    .sel(compare16_1_1_r), .in_0({16{1'b0}}), .in_1({16{1'b1}}), .out(multiplexer_17_out));
  Multiplexer #(.Bits(16)) multiplexer_18 (
    .sel(opcode[6]), .in_0(multiplexer_16_out), .in_1(multiplexer_17_out), .out(multiplexer_18_out));
  Multiplexer #(.Bits(16)) multiplexer_19 (
    .sel(opcode[7]), .in_0(multiplexer_15_out), .in_1(multiplexer_18_out), .out(R));

  // Notes on the sheet:
  //   arithmetic
  //   logic
  //   comparison
endmodule

/* Test case arithmetic tests:
opcode           A       B       R
# addition
# RXsYsAluop*AB
0b0000000000000  0x0000  0x0000  0x0000
0b0000000000000  0x0001  0x0000  0x0001
0b0000000000000  0x0000  0x0001  0x0001
0b0000000000000  0x0001  0x0001  0x0002
0b0000000000000  0x0002  0x0003  0x0005

# subtraction
# RXsYsAluop*AB
0b0000000001000  0x0000  0x0000  0x0000
0b0000000001000  0x0001  0x0000  0x0001
0b0000000001000  0x0001  0x0001  0x0000
0b0000000001000  0x0002  0x0001  0x0001
0b0000000001000  0x0002  0x0000  0x0002
0b0000000001000  0x0001  0x0002  0xFFFF
0b0000000001000  0x0000  0x0001  0xFFFF
0b0000000001000  0x0000  0x0002  0xFFFE

# multiplication
# RXsYsAluop*AB
0b0000000010000  0x0000  0x0000  0x0000
0b0000000010000  0x0001  0x0000  0x0000
0b0000000010000  0x0000  0x0001  0x0000
0b0000000010000  0x0001  0x0001  0x0001
0b0000000010000  0x0000  0x0002  0x0000
0b0000000010000  0x0002  0x0000  0x0000
0b0000000010000  0x0002  0x0002  0x0004
0b0000000010000  0x0002  0x0001  0x0002
0b0000000010000  0x0001  0x0002  0x0002
0b0000000010000  0xFFFF  0x0002  0xFFFE
0b0000000010000  0x0002  0xFFFF  0xFFFE

# division
# RXsYsAluop*AB
0b0000000011000  0x0000  0x0000  X

0b0000000011000  0x0001  0x0001  0x0001
0b0000000011000  0x0002  0x0001  0x0002
0b0000000011000  0x0003  0x0001  0x0003
0b0000000011000  0x0004  0x0001  0x0004
0b0000000011000  0x0005  0x0001  0x0005
0b0000000011000  0x0006  0x0001  0x0006
0b0000000011000  0x0007  0x0001  0x0007

0b0000000011000  0x0001  0x0002  0x0000
0b0000000011000  0x0002  0x0002  0x0001
0b0000000011000  0x0003  0x0002  0x0001
0b0000000011000  0x0004  0x0002  0x0002
0b0000000011000  0x0005  0x0002  0x0002
0b0000000011000  0x0006  0x0002  0x0003
0b0000000011000  0x0007  0x0002  0x0003

# shift left
# RXsYsAluop*AB
0b0000000100000  0x0000  0x0000  0x0000
0b0000000100000  0x0000  0x0001  0x0000
0b0000000100000  0x0000  0x0002  0x0000
0b0000000100000  0x0001  0x0000  0x0001
0b0000000100000  0x0001  0x0001  0x0002
0b0000000100000  0x0001  0x0002  0x0004
0b0000000100000  0x0002  0x0000  0x0002
0b0000000100000  0x0002  0x0001  0x0004
0b0000000100000  0x0002  0x0002  0x0008
0b0000000100000  0x0003  0x0000  0x0003
0b0000000100000  0x0003  0x0001  0x0006
0b0000000100000  0x0003  0x0002  0x000C

# shift right
# RXsYsAluop*AB
0b0000000101000  0x0000  0x0000  0x0000
0b0000000101000  0x0000  0x0001  0x0000
0b0000000101000  0x0000  0x0002  0x0000
0b0000000101000  0x0002  0x0000  0x0002
0b0000000101000  0x0002  0x0001  0x0001
0b0000000101000  0x0002  0x0002  0x0000
0b0000000101000  0x0003  0x0000  0x0003
0b0000000101000  0x0003  0x0001  0x0001
0b0000000101000  0x0003  0x0002  0x0000
0b0000000101000  0x0004  0x0000  0x0004
0b0000000101000  0x0004  0x0001  0x0002
0b0000000101000  0x0004  0x0002  0x0001
*/

/* Test case bitwise tests:
opcode            A       B       R
# bitwise and
# RXsYsAluop*AB
0b0000010000000  0x0000  0x0000  0x0000
0b0000010000000  0x0000  0x0001  0x0000
0b0000010000000  0x0001  0x0000  0x0000
0b0000010000000  0x0001  0x0001  0x0001
0b0000010000000  0x0002  0x0001  0x0000
0b0000010000000  0x0001  0x0002  0x0000
0b0000010000000  0x0002  0x0002  0x0002
0b0000010000000  0x0002  0x0000  0x0000
0b0000010000000  0x0000  0x0002  0x0000
0b0000010000000  0x0003  0x0002  0x0002

# bitwise or
# RXsYsAluop*AB
0b0000010001000  0x0000  0x0000  0x0000
0b0000010001000  0x0000  0x0001  0x0001
0b0000010001000  0x0001  0x0000  0x0001
0b0000010001000  0x0001  0x0001  0x0001
0b0000010001000  0x0002  0x0001  0x0003
0b0000010001000  0x0001  0x0002  0x0003
0b0000010001000  0x0002  0x0002  0x0002
0b0000010001000  0x0002  0x0000  0x0002
0b0000010001000  0x0000  0x0002  0x0002
0b0000010001000  0x0003  0x0002  0x0003

# bitwise not x
# RXsYsAluop*AB
0b0000010010000  0x0000  0x0000  0xFFFF
0b0000010010000  0x0000  0x0001  0xFFFF
0b0000010010000  0x0001  0x0000  0xFFFE
0b0000010010000  0x0001  0x0001  0xFFFE
0b0000010010000  0x0002  0x0000  0xFFFD
0b0000010010000  0x0002  0x0001  0xFFFD
0b0000010010000  0x0003  0x0000  0xFFFC
0b0000010010000  0x0003  0x0001  0xFFFC
0b0000010010000  0x0004  0x0000  0xFFFB
0b0000010010000  0x0004  0x0001  0xFFFB

# bitwise not y
# RXsYsAluop*AB
0b0000010011000  0x0000  0x0000  0xFFFF
0b0000010011000  0x0001  0x0000  0xFFFF
0b0000010011000  0x0000  0x0001  0xFFFE
0b0000010011000  0x0001  0x0001  0xFFFE
0b0000010011000  0x0000  0x0002  0xFFFD
0b0000010011000  0x0001  0x0002  0xFFFD
0b0000010011000  0x0000  0x0003  0xFFFC
0b0000010011000  0x0001  0x0003  0xFFFC
0b0000010011000  0x0000  0x0004  0xFFFB
0b0000010011000  0x0001  0x0004  0xFFFB

# bitwise xor
# RXsYsAluop*AB
0b0000010100000  0x0000  0x0000  0x0000
0b0000010100000  0x0001  0x0000  0x0001
0b0000010100000  0x0000  0x0001  0x0001
0b0000010100000  0x0001  0x0001  0x0000
0b0000010100000  0x0000  0x0002  0x0002
0b0000010100000  0x0001  0x0002  0x0003
0b0000010100000  0x0000  0x0003  0x0003
0b0000010100000  0x0001  0x0003  0x0002
0b0000010100000  0x0000  0x0004  0x0004

# bitwise xnor
# RXsYsAluop*AB
0b0000010101000  0x0000  0x0000  0xFFFF
0b0000010101000  0x0001  0x0000  0xFFFE
0b0000010101000  0x0000  0x0001  0xFFFE
0b0000010101000  0x0001  0x0001  0xFFFF
0b0000010101000  0x0000  0x0002  0xFFFD
0b0000010101000  0x0001  0x0002  0xFFFC
0b0000010101000  0x0000  0x0003  0xFFFC
0b0000010101000  0x0001  0x0003  0xFFFD
0b0000010101000  0x0000  0x0004  0xFFFB

# bitwise nor
# RXsYsAluop*AB
0b0000010110000  0x0000  0x0000  0xFFFF
0b0000010110000  0x0001  0x0000  0xFFFE
0b0000010110000  0x0000  0x0001  0xFFFE
0b0000010110000  0x0001  0x0001  0xFFFE
0b0000010110000  0x0000  0x0002  0xFFFD
0b0000010110000  0x0001  0x0002  0xFFFC
0b0000010110000  0x0000  0x0003  0xFFFC
0b0000010110000  0x0001  0x0003  0xFFFC
0b0000010110000  0x0000  0x0004  0xFFFB

# bitwise nand
# RXsYsAluop*AB
0b0000010111000  0x0000  0x0000  0xFFFF
0b0000010111000  0x0001  0x0000  0xFFFF
0b0000010111000  0x0000  0x0001  0xFFFF
0b0000010111000  0x0001  0x0001  0xFFFE
0b0000010111000  0x0000  0x0002  0xFFFF
0b0000010111000  0x0001  0x0002  0xFFFF
0b0000010111000  0x0000  0x0003  0xFFFF
0b0000010111000  0x0001  0x0003  0xFFFE
0b0000010111000  0x0000  0x0004  0xFFFF
*/

/* Test case comparison tests:
opcode            A       B       R
# false
# RXsYsAluop*AB
0b0000011000000  0x0000  0x0000  0x0000
0b0000011000000  0x0000  0x0001  0x0000
0b0000011000000  0x0001  0x0000  0x0000
0b0000011000000  0x0001  0x0001  0x0000
0b0000011000000  0x0002  0x0001  0x0000
0b0000011000000  0x0001  0x0002  0x0000
0b0000011000000  0x0002  0x0002  0x0000
0b0000011000000  0x0002  0x0000  0x0000
0b0000011000000  0x0000  0x0002  0x0000
0b0000011000000  0x0003  0x0002  0x0000

# greater than
# RXsYsAluop*AB
0b0000011001000  0x0000  0x0000  0x0000
0b0000011001000  0x0000  0x0001  0x0000
0b0000011001000  0x0001  0x0000  0xFFFF
0b0000011001000  0x0001  0x0001  0x0000
0b0000011001000  0x0002  0x0001  0xFFFF
0b0000011001000  0x0001  0x0002  0x0000
0b0000011001000  0x0002  0x0002  0x0000
0b0000011001000  0x0002  0x0000  0xFFFF
0b0000011001000  0x0000  0x0002  0x0000
0b0000011001000  0x0003  0x0002  0xFFFF

# equals
# RXsYsAluop*AB
0b0000011010000  0x0000  0x0000  0xFFFF
0b0000011010000  0x0000  0x0001  0x0000
0b0000011010000  0x0001  0x0000  0x0000
0b0000011010000  0x0001  0x0001  0xFFFF
0b0000011010000  0x0002  0x0001  0x0000
0b0000011010000  0x0001  0x0002  0x0000
0b0000011010000  0x0002  0x0002  0xFFFF
0b0000011010000  0x0002  0x0000  0x0000
0b0000011010000  0x0000  0x0002  0x0000
0b0000011010000  0x0003  0x0002  0x0000

# greater than or equals
# RXsYsAluop*AB
0b0000011011000  0x0000  0x0000  0xFFFF
0b0000011011000  0x0000  0x0001  0x0000
0b0000011011000  0x0001  0x0000  0xFFFF
0b0000011011000  0x0001  0x0001  0xFFFF
0b0000011011000  0x0002  0x0001  0xFFFF
0b0000011011000  0x0001  0x0002  0x0000
0b0000011011000  0x0002  0x0002  0xFFFF
0b0000011011000  0x0002  0x0000  0xFFFF
0b0000011011000  0x0000  0x0002  0x0000
0b0000011011000  0x0003  0x0002  0xFFFF

# less than
# RXsYsAluop*AB
0b0000011100000  0x0000  0x0000  0x0000
0b0000011100000  0x0000  0x0001  0xFFFF
0b0000011100000  0x0001  0x0000  0x0000
0b0000011100000  0x0001  0x0001  0x0000
0b0000011100000  0x0002  0x0001  0x0000
0b0000011100000  0x0001  0x0002  0xFFFF
0b0000011100000  0x0002  0x0002  0x0000
0b0000011100000  0x0002  0x0000  0x0000
0b0000011100000  0x0000  0x0002  0xFFFF
0b0000011100000  0x0003  0x0002  0x0000

# less than or equals
# RXsYsAluop*AB
0b0000011110000  0x0000  0x0000  0xFFFF
0b0000011110000  0x0000  0x0001  0xFFFF
0b0000011110000  0x0001  0x0000  0x0000
0b0000011110000  0x0001  0x0001  0xFFFF
0b0000011110000  0x0002  0x0001  0x0000
0b0000011110000  0x0001  0x0002  0xFFFF
0b0000011110000  0x0002  0x0002  0xFFFF
0b0000011110000  0x0002  0x0000  0x0000
0b0000011110000  0x0000  0x0002  0xFFFF
0b0000011110000  0x0003  0x0002  0x0000

# not equals
# RXsYsAluop*AB
0b0000011101000  0x0000  0x0000  0x0000
0b0000011101000  0x0000  0x0001  0xFFFF
0b0000011101000  0x0001  0x0000  0xFFFF
0b0000011101000  0x0001  0x0001  0x0000
0b0000011101000  0x0002  0x0001  0xFFFF
0b0000011101000  0x0001  0x0002  0xFFFF
0b0000011101000  0x0002  0x0002  0x0000
0b0000011101000  0x0002  0x0000  0xFFFF
0b0000011101000  0x0000  0x0002  0xFFFF
0b0000011101000  0x0003  0x0002  0xFFFF
*/

/* Test case selection tests:
opcode            A       B       *Ax     R
# RXsYsAluop*AB
0b0000000000000  0x0003  0x0005  0x0009  0x0008

0b0010000000000  0x0003  0x0005  0x0009  0x0005
0b0100000000000  0x0003  0x0005  0x0009  0x0006
0b0110000000000  0x0003  0x0005  0x0009  0x000E

0b0000100000000  0x0003  0x0005  0x0009  0x0003
0b0001000000000  0x0003  0x0005  0x0009  0x0004
0b0001100000000  0x0003  0x0005  0x0009  0x000C

0b0010100000000  0x0003  0x0005  0x0009  0x0000
0b0011000000000  0x0003  0x0005  0x0009  0x0001
0b0011100000000  0x0003  0x0005  0x0009  0x0009

0b0100100000000  0x0003  0x0005  0x0009  0x0001
0b0101000000000  0x0003  0x0005  0x0009  0x0002
0b0101100000000  0x0003  0x0005  0x0009  0x000A

0b0110100000000  0x0003  0x0005  0x0009  0x0009
0b0111000000000  0x0003  0x0005  0x0009  0x000A
0b0111100000000  0x0003  0x0005  0x0009  0x0012


0b1000000000000  0x0003  0x0005  0x0009  0x0008

0b1010000000000  0x0003  0x0005  0x0009  0x0003
0b1100000000000  0x0003  0x0005  0x0009  0x0004
0b1110000000000  0x0003  0x0005  0x0009  0x000C

0b1000100000000  0x0003  0x0005  0x0009  0x0005
0b1001000000000  0x0003  0x0005  0x0009  0x0006
0b1001100000000  0x0003  0x0005  0x0009  0x000E

0b1010100000000  0x0003  0x0005  0x0009  0x0000
0b1011000000000  0x0003  0x0005  0x0009  0x0001
0b1011100000000  0x0003  0x0005  0x0009  0x0009

0b1100100000000  0x0003  0x0005  0x0009  0x0001
0b1101000000000  0x0003  0x0005  0x0009  0x0002
0b1101100000000  0x0003  0x0005  0x0009  0x000A

0b1110100000000  0x0003  0x0005  0x0009  0x0009
0b1111000000000  0x0003  0x0005  0x0009  0x000A
0b1111100000000  0x0003  0x0005  0x0009  0x0012
*/
