// Digital circuit alu16_2_operands.dig as structural Verilog
module alu16_2_operands (
  input  [15:0] A,
  input  [15:0] B,
  input  [15:0] Ax,
  input  Rsel,
  input  [1:0] Xsel,
  input  [1:0] Ysel,
  output [15:0] X,
  output [15:0] Y
);

  wire [15:0] multiplexer_1_out, multiplexer_2_out;

  Multiplexer #(.Bits(16)) multiplexer_1 (.sel(Rsel), .in_0(A), .in_1(B), .out(multiplexer_1_out));
  Multiplexer #(.Bits(16)) multiplexer_2 (.sel(Rsel), .in_0(B), .in_1(A), .out(multiplexer_2_out));
  Multiplexer #(.Selector_Bits(2), .Bits(16)) multiplexer_3 (
    .sel(Xsel), .in_0(multiplexer_1_out), .in_1({16{1'b0}}), .in_2(16'h1), .in_3(Ax), .out(X));
  Multiplexer #(.Selector_Bits(2), .Bits(16)) multiplexer_4 (
    .sel(Ysel), .in_0(multiplexer_2_out), .in_1({16{1'b0}}), .in_2(16'h1), .in_3(Ax), .out(Y));
endmodule

/* Test case tests:
# yes, the column layout is illogical, feel free to fix it.
    Xsel Ysel Rsel X   Y   *Ax A   B

loop(m,4)
  loop(i,5)
    let a = random(0xffff);
    let b = random(0xffff);
    let c = random(0xffff);
    
    0b00 0b00 0    (a) (b) (c) (a) (b)
    0b00 0b01 0    (a) 0   (c) (a) (b)
    0b00 0b10 0    (a) 1   (c) (a) (b)
    0b00 0b11 0    (a) (c) (c) (a) (b)

    0b01 0b00 0    0   (b) (c) (a) (b)
    0b01 0b01 0    0   0   (c) (a) (b)
    0b01 0b10 0    0   1   (c) (a) (b)
    0b01 0b11 0    0   (c) (c) (a) (b)

    0b10 0b00 0    1   (b) (c) (a) (b)
    0b10 0b01 0    1   0   (c) (a) (b)
    0b10 0b10 0    1   1   (c) (a) (b)
    0b10 0b11 0    1   (c) (c) (a) (b)

    0b11 0b00 0    (c) (b) (c) (a) (b)
    0b11 0b01 0    (c) 0   (c) (a) (b)
    0b11 0b10 0    (c) 1   (c) (a) (b)
    0b11 0b11 0    (c) (c) (c) (a) (b)


    
    0b00 0b00 1    (a) (b) (c) (b) (a)
    0b00 0b01 1    (a) 0   (c) (b) (a)
    0b00 0b10 1    (a) 1   (c) (b) (a)
    0b00 0b11 1    (a) (c) (c) (b) (a)

    0b01 0b00 1    0   (b) (c) (b) (a)
    0b01 0b01 1    0   0   (c) (b) (a)
    0b01 0b10 1    0   1   (c) (b) (a)
    0b01 0b11 1    0   (c) (c) (b) (a)

    0b10 0b00 1    1   (b) (c) (b) (a)
    0b10 0b01 1    1   0   (c) (b) (a)
    0b10 0b10 1    1   1   (c) (b) (a)
    0b10 0b11 1    1   (c) (c) (b) (a)

    0b11 0b00 1    (c) (b) (c) (b) (a)
    0b11 0b01 1    (c) 0   (c) (b) (a)
    0b11 0b10 1    (c) 1   (c) (b) (a)
    0b11 0b11 1    (c) (c) (c) (b) (a)
  end loop
end loop
*/
