// Digital circuit compare16_1.dig as structural Verilog
module compare16_1 (
  input  [15:0] A,
  input  [15:0] B,
  input  [2:0] m,
  output r
);

  wire and_1_out, and_2_out, and_3_out, comparator_1_eq, comparator_1_gt, comparator_1_lt;

  Comparator #(.Signed("true"), .Bits(16)) comparator_1 (
    .a(A), .b(B), .gt(comparator_1_gt), .eq(comparator_1_eq), .lt(comparator_1_lt));
  and and_1 (and_1_out, m[0], comparator_1_gt);
  and and_2 (and_2_out, m[1], comparator_1_eq);
  and and_3 (and_3_out, m[2], comparator_1_lt);
  or or_1 (r, and_1_out, and_2_out, and_3_out);
endmodule

/* Test case comparison tests:
m      A       B       r
# false
0b000  0x0000  0x0000  0
0b000  0x0000  0x0001  0
0b000  0x0001  0x0000  0
0b000  0x0001  0x0001  0
0b000  0x0002  0x0001  0
0b000  0x0001  0x0002  0
0b000  0x0002  0x0002  0
0b000  0x0002  0x0000  0
0b000  0x0000  0x0002  0
0b000  0x0003  0x0002  0

# greater than
0b001  0x0000  0x0000  0
0b001  0x0000  0x0001  0
0b001  0x0001  0x0000  1
0b001  0x0001  0x0001  0
0b001  0x0002  0x0001  1
0b001  0x0001  0x0002  0
0b001  0x0002  0x0002  0
0b001  0x0002  0x0000  1
0b001  0x0000  0x0002  0
0b001  0x0003  0x0002  1

# equals
0b010  0x0000  0x0000  1
0b010  0x0000  0x0001  0
0b010  0x0001  0x0000  0
0b010  0x0001  0x0001  1
0b010  0x0002  0x0001  0
0b010  0x0001  0x0002  0
0b010  0x0002  0x0002  1
0b010  0x0002  0x0000  0
0b010  0x0000  0x0002  0
0b010  0x0003  0x0002  0

# greater than or equals
0b011  0x0000  0x0000  1
0b011  0x0000  0x0001  0
0b011  0x0001  0x0000  1
0b011  0x0001  0x0001  1
0b011  0x0002  0x0001  1
0b011  0x0001  0x0002  0
0b011  0x0002  0x0002  1
0b011  0x0002  0x0000  1
0b011  0x0000  0x0002  0
0b011  0x0003  0x0002  1

# less than
0b100  0x0000  0x0000  0
0b100  0x0000  0x0001  1
0b100  0x0001  0x0000  0
0b100  0x0001  0x0001  0
0b100  0x0002  0x0001  0
0b100  0x0001  0x0002  1
0b100  0x0002  0x0002  0
0b100  0x0002  0x0000  0
0b100  0x0000  0x0002  1
0b100  0x0003  0x0002  0

# less than or equals
0b110  0x0000  0x0000  1
0b110  0x0000  0x0001  1
0b110  0x0001  0x0000  0
0b110  0x0001  0x0001  1
0b110  0x0002  0x0001  0
0b110  0x0001  0x0002  1
0b110  0x0002  0x0002  1
0b110  0x0002  0x0000  0
0b110  0x0000  0x0002  1
0b110  0x0003  0x0002  0

# not equals
0b101  0x0000  0x0000  0
0b101  0x0000  0x0001  1
0b101  0x0001  0x0000  1
0b101  0x0001  0x0001  0
0b101  0x0002  0x0001  1
0b101  0x0001  0x0002  1
0b101  0x0002  0x0002  0
0b101  0x0002  0x0000  1
0b101  0x0000  0x0002  1
0b101  0x0003  0x0002  1

# true
0b111  0x0000  0x0000  1
0b111  0x0000  0x0001  1
0b111  0x0001  0x0000  1
0b111  0x0001  0x0001  1
0b111  0x0002  0x0001  1
0b111  0x0001  0x0002  1
0b111  0x0002  0x0002  1
0b111  0x0002  0x0000  1
0b111  0x0000  0x0002  1
0b111  0x0003  0x0002  1
*/
