// Digital circuit computer_proc16a2_mappedmemory.dig as structural Verilog
module computer_proc16a2_mappedmemory (
  input  programClock,
  input  stopClock,
  input  startClock,
  input  [15:0] At_2,
  output [15:0] At
);

  wire and_1_out, and_2_out, and_3_out, and_4_out, \break , clock, cpu_proc16a2_1_p9, cpu_proc16a2_1_p10,
       d_ff_1_q, demultiplexer_3_out_1, demultiplexer_4_out_1, enable_dev, enable_dev_btn,
       enable_dev_fbswitch, enable_gram, enable_ram, jump, not_1_out, or_1_out, register_1_q,
       reset_break_led_out, rs_ff_as_1_q, rs_ff_as_2_q, step_out, wA;
  wire [7:0] C_out;
  wire [15:0] A, addr, addr_dec, counterpreset_1_out, instruction, out_dev, out_gram, out_proc, out_ram,
       ramdualport_1_d;

  or or_1 (or_1_out, stopClock, d_ff_1_q);
  Break #(.Cycles(1000000)) break_1 (.brk(d_ff_1_q));
  RS_FF_AS rs_ff_as_1 (.S(d_ff_1_q), .R(reset_break_led_out), .Q(rs_ff_as_1_q));  // open: nQ
  Button LEFT (.out(C_out[5]));
  RS_FF_AS rs_ff_as_2 (.S(startClock), .R(or_1_out), .Q(rs_ff_as_2_q));  // open: nQ
  LED led_1 (.in(rs_ff_as_1_q));
  Button reset_break_led (.out(reset_break_led_out));
  D_FF d_ff_1 (.D(\break ), .C(clock), .Q(d_ff_1_q));  // open: nQ
  Button UP (.out(C_out[7]));
  Button DOWN (.out(C_out[6]));
  and and_1 (and_1_out, programClock, rs_ff_as_2_q);
  Button RIGHT (.out(C_out[4]));
  Button step (.out(step_out));
  Button B (.out(C_out[2]));
  or or_2 (clock, and_1_out, step_out);
  Button u_A (.out(C_out[3]));
  Button C (.out(C_out[1]));
  Button D (.out(C_out[0]));
  assign out_dev = enable_dev_btn ? {{8{1'b0}}, C_out} : 16'bz;  // Driver driver_1
  RAMDualAccess #(.AddrBits(16), .Bits(16)) ramdualaccess_1 (
    .str(wA), .C(clock), .ld(1'b1), .A1(addr), .Din1(out_proc), .A2(At_2), .D2(At));  // open: D1
  Seven_Seg_Hex seven_seg_hex_1 (.d(At[15:12]), .dp(1'b0));
  CounterPreset #(.Bits(16), .isProgramCounter("true")) counterpreset_1 (
    .en(1'b1), .C(clock), .dir(1'b0), .in(out_proc), .ld(jump), .clr(1'b0), .out(counterpreset_1_out));  // open: ovf
  Demultiplexer demultiplexer_1 (
    .sel(addr_dec[0]), .in(enable_dev), .out_0(enable_dev_btn), .out_1(enable_dev_fbswitch));
  Seven_Seg_Hex seven_seg_hex_2 (.d(At[11:8]), .dp(1'b0));
  // Probe PC on counterpreset_1_out
  ROM #(.bigEndian("true"), .AddrBits(16), .isProgramMemory("true"), .Bits(16)) rom_1 (
    .A(counterpreset_1_out), .sel(1'b1), .D(instruction));
  Seven_Seg_Hex seven_seg_hex_3 (.d(At[7:4]), .dp(1'b0));
  // Probe I on instruction
  Demultiplexer demultiplexer_2 (.sel(addr[13]), .in(demultiplexer_3_out_1), .out_1(enable_dev));  // open: out_0
  Demultiplexer demultiplexer_3 (
    .sel(addr[13]), .in(demultiplexer_4_out_1), .out_0(enable_gram), .out_1(demultiplexer_3_out_1));
  Demultiplexer demultiplexer_4 (.sel(addr[14]), .in(1'b1), .out_0(enable_ram), .out_1(demultiplexer_4_out_1));
  Seven_Seg_Hex seven_seg_hex_4 (.d(At[3:0]), .dp(1'b0));
  // cpu_proc16a2 cpu_proc16a2_1: pin names not known; wires that end beside it: clock, A, instruction, jump, wA, addr, out_proc, \break , cpu_proc16a2_1_p9, cpu_proc16a2_1_p10
  // Probe out_proc on out_proc
  // Probe on out_proc
  // Probe on out_proc
  assign addr_dec = enable_dev ? {3'b000, addr[12:0]} : 16'bz;  // Driver driver_2
  assign addr_dec = enable_gram ? {3'b000, addr[12:0]} : 16'bz;  // Driver driver_3
  assign addr_dec = enable_ram ? {2'b00, addr[13:0]} : 16'bz;  // Driver driver_4
  assign A = enable_dev ? out_dev : 16'bz;  // Driver driver_5
  assign A = enable_gram ? out_gram : 16'bz;  // Driver driver_6
  assign A = enable_ram ? out_ram : 16'bz;  // Driver driver_7
  // Probe test_B on cpu_proc16a2_1_p9
  // Probe on cpu_proc16a2_1_p9
  // Probe on cpu_proc16a2_1_p9
  // Probe test_A on cpu_proc16a2_1_p10
  // Probe on cpu_proc16a2_1_p10
  // Probe on cpu_proc16a2_1_p10
  // Probe A on addr
  // Probe on addr
  // Probe on addr
  and and_2 (and_2_out, enable_ram, wA);
  and and_3 (and_3_out, enable_dev_fbswitch, wA);
  and and_4 (and_4_out, enable_gram, wA);
  not not_1 (not_1_out, wA);
  Register register_1 (.D(out_proc[0]), .C(clock), .en(and_3_out), .Q(register_1_q));
  RAMDualPort #(.AddrBits(14), .Bits(16)) ramdualport_1 (
    .A(addr_dec[13:0]), .Din(out_proc), .str(and_2_out), .C(clock), .ld(1'b1), .D(ramdualport_1_d));
  GraphicCard #(.graphicHeight(64), .graphicWidth(64), .Bits(16)) graphiccard_1 (
    .A(addr_dec[12:0]), .str(and_4_out), .C(clock), .ld(not_1_out), .B(register_1_q), .D(out_gram));
  assign out_ram = enable_ram ? ramdualport_1_d : 16'bz;  // Driver driver_8
  assign out_gram = and_4_out ? out_proc : 16'bz;  // Driver driver_9

  // Notes on the sheet:
  //   programClock: Hz: 1000
  //   clock
  //   Address map:
  //   0x0000 - 0x3FFF (16Ki) RAM
  //   0x4000 - 0x5FFF (8Ki) video memory
  //   0x6000 - 0x7FFF (8Ki) devices
  //   0x8000 - 0xFFFF (32Ki) unusable
  //   devices:
  //   0x6000: button inputs
  //   0x6001: framebuffer switch
  //   button device
  //   bits 15-8 are 0
  //   7 6543210
  //   UDLRABXY
  //   address bus test instrumentation
  //   program memory
  //   primary address decoder
  //   device address decoder
  //   contents of rom_1 (hex, n*v repeats v):
  //   6000,8d02,0,9104,0,a00f
  //   cpu
  //   RAM
  //   graphic RAM + fbswitch device
  //   fbswitch device:
  //   bit 0 is a 1-bit register that
  //   controls the active framebuffer
  //   all other bits are unconnected
endmodule

/* Test case increment forever:
startClock programClock PC test_A test_B

program(0x0000, 0x8A02, 0x8201, 0xA001)

1 0  0x0000  X       X
0 C  0x0001  0x0000  X
0 C  0x0002  0x0000  0x0002
0 C  0x0003  0x0001  0x0002
0 C  0x0002  0x0001  0x0002
0 C  0x0003  0x0002  0x0002
0 C  0x0002  0x0002  0x0002
0 C  0x0003  0x0003  0x0002
0 C  0x0002  0x0003  0x0002
0 C  0x0003  0x0004  0x0002
0 C  0x0002  0x0004  0x0002
0 C  0x0003  0x0005  0x0002
0 C  0x0002  0x0005  0x0002
0 C  0x0003  0x0006  0x0002
*/

/* Test case fill ram cells with address:
startClock programClock PC I At *At

program(0x8502, 0xD104, 0x9202, 0x0001, 0xA00F)

1 0 0x0000  0x8502  0       X

loop(i, 16)
1 C 0x0001  0xD104  0       X
1 C 0x0002  0x9202  0       X
1 C 0x0003  0x0001  0       X
1 C 0x0004  0xA00F  0       X
end loop

loop(j, 16)
1 0 X  X  (j)  (j)
end loop
*/

/* Test case compute fibonacci:
startClock programClock At *At PC

program(0x0001, 0x8904, 0x8201, 0x8904, 0x8102, 0x0000, 0x9104, 0x0000, 0x8D01, 0x8D02, 0x8209, 0x8D01, 0x8002, 0x0000, 0x8D01, 0x8201, 0x9104, 0x0000, 0x8E04, 0x0007, 0xA00F)

1 0 0 0 x

loop(i, 6)
  0 C 0xFFFF 0 x
end loop

0 C 0x0000 2 7


loop(j, 11)
  0 C 0xFFFF 0 x
end loop

0 C 0 3 19
0 C 3 2 20



loop(j, 12)
  0 C 0xFFFF 0 x
end loop

0 C 0 4 x
0 C 4 3 x



loop(j, 12)
  0 C 0xFFFF 0 x
end loop

0 C 0 5 x
0 C 5 5 x
######


loop(j, 12)
  0 C 0xFFFF 0 x
end loop

0 C 0 6 x
0 C 6 8 x



loop(j, 12)
  0 C 0xFFFF 0 x
end loop

0 C 0 7 x
0 C 7 13 x



loop(j, 12)
  0 C 0xFFFF 0 x
end loop

0 C 0 8 x
0 C 8 21 x



loop(j, 12)
  0 C 0xFFFF 0 x
end loop

0 C 0 9 x
0 C 9 34 x



loop(j, 12)
  0 C 0xFFFF 0 x
end loop

0 C 0 10 x
0 C 10 55 x



loop(j, 12)
  0 C 0xFFFF 0 x
end loop

0 C 0 11 x
0 C 11 89 x



loop(j, 12)
  0 C 0xFFFF 0 x
end loop

0 C 0 12 x
0 C 12 144 x



loop(j, 12)
  0 C 0xFFFF 0 x
end loop

0 C 0 13 x
0 C 13 233 x



loop(j, 12)
  0 C 0xFFFF 0 x
end loop

0 C 0 14 x
0 C 14 377 x



loop(j, 12)
  0 C 0xFFFF 0 x
end loop

0 C 0 15 x
0 C 15 610 x



loop(j, 12)
  0 C 0xFFFF 0 x
end loop

0 C 0 16 x
0 C 16 987 x
*/
