// Digital circuit proc16a1.dig as structural Verilog
module proc16a1 (
  input  programClock,
  input  stopClock,
  input  startClock,
  input  [15:0] At,
  input  testRamClock,
  output [15:0] mAt
);

  wire and_1_out, jump16_1_1_j, not_1_out, or_1_out, or_2_out, or_3_out, or_4_out, or_5_out, reset_PC_out,
       rs_ff_as_1_q, step_out;
  wire [10:0] demultiplexer_3_out_0, demultiplexer_3_out_1;
  wire [12:0] demultiplexer_2_out_0, demultiplexer_2_out_1;
  wire [14:0] demultiplexer_1_out_0, demultiplexer_1_out_1;
  wire [15:0] ALU_r, jump16_1_1_ai, multiplexer_1_out, multiplexer_2_out, programCounter_out, R_A_q, R_B_q,
       RAM_d, rom_1_d;

  RS_FF_AS rs_ff_as_1 (.S(startClock), .R(or_1_out), .Q(rs_ff_as_1_q));  // open: nQ
  or or_1 (or_1_out, stopClock, demultiplexer_3_out_1[0]);
  and and_1 (and_1_out, programClock, rs_ff_as_1_q);
  Button step (.out(step_out));
  Button reset_PC (.out(reset_PC_out));
  or or_2 (or_2_out, and_1_out, or_3_out);
  or or_3 (or_3_out, step_out, reset_PC_out);
  RAMDualAccess #(.AddrBits(16), .Bits(16)) test_RAM (
    .str(demultiplexer_2_out_0[2]), .C(or_4_out), .ld(1'b1), .A1(multiplexer_1_out),
    .Din1(multiplexer_2_out), .A2(At), .D2(mAt));  // open: D1
  or or_4 (or_4_out, testRamClock, or_2_out);
  CounterPreset #(.Bits(16), .isProgramCounter("true")) programCounter (
    .en(1'b1), .C(or_2_out), .dir(1'b0), .in(jump16_1_1_ai), .ld(jump16_1_1_j), .clr(reset_PC_out),
    .out(programCounter_out));  // open: ovf
  Register #(.Bits(16)) R_A (.D(multiplexer_2_out), .C(or_2_out), .en(or_5_out), .Q(R_A_q));
  Register #(.Bits(16)) R_B (.D(multiplexer_2_out), .C(or_2_out), .en(demultiplexer_2_out_0[1]), .Q(R_B_q));
  RAMDualPort #(.AddrBits(16), .Bits(16)) RAM (
    .A(multiplexer_1_out), .Din(multiplexer_2_out), .str(demultiplexer_2_out_0[2]), .C(or_2_out), .ld(1'b1),
    .D(RAM_d));
  // Probe instructionPointer on programCounter_out
  ROM #(.AddrBits(16), .isProgramMemory("true"), .Bits(16)) rom_1 (.A(programCounter_out), .sel(1'b1), .D(rom_1_d));
  Multiplexer #(.Bits(16)) multiplexer_1 (
    .sel(demultiplexer_1_out_1[14]), .in_0(R_A_q), .in_1(R_B_q), .out(multiplexer_1_out));
  // Probe Ax on multiplexer_1_out
  // Probe A on R_A_q
  // Probe on R_A_q
  Break break_1 (.brk(demultiplexer_3_out_1[0]));
  // Probe instruction on rom_1_d
  // Probe B on R_B_q
  // Probe on R_B_q
  Demultiplexer #(.Bits(15)) demultiplexer_1 (
    .sel(rom_1_d[15]), .in(rom_1_d[14:0]), .out_0(demultiplexer_1_out_0), .out_1(demultiplexer_1_out_1));
  // Probe mAx on RAM_d
  // Probe on RAM_d
  or or_5 (or_5_out, demultiplexer_2_out_0[0], not_1_out);
  not not_1 (not_1_out, rom_1_d[15]);
  Demultiplexer #(.Bits(13)) demultiplexer_2 (
    .sel(demultiplexer_1_out_1[13]), .in(demultiplexer_1_out_1[12:0]), .out_0(demultiplexer_2_out_0),
    .out_1(demultiplexer_2_out_1));
  Demultiplexer #(.Bits(11)) demultiplexer_3 (
    .sel(demultiplexer_2_out_1[11]), .in(demultiplexer_2_out_1[10:0]), .out_0(demultiplexer_3_out_0),
    .out_1(demultiplexer_3_out_1));
  alu16_2 ALU (.opcode(demultiplexer_2_out_0), .A(R_A_q), .B(R_B_q), .Ax(RAM_d), .R(ALU_r));
  jump16_1 jump16_1_1 (.A(R_A_q), .B(R_B_q), .I(demultiplexer_3_out_0), .j(jump16_1_1_j), .Ai(jump16_1_1_ai));
  Multiplexer #(.Bits(16)) multiplexer_2 (
    .sel(rom_1_d[15]), .in_0({1'b0, demultiplexer_1_out_0}), .in_1(ALU_r), .out(multiplexer_2_out));
  // Probe output on multiplexer_2_out
  // also tied to GND on the sheet: demultiplexer_2_out_1[12]

  // Notes on the sheet:
  //   programClock: Hz: 10
  //   Clock
  //   test instrumentation
  //   contents of rom_1 (hex, n*v repeats v):
  //   1,8904,8201,8904,8102,0,9104,0,8d01,8d02,8209,8d01,8002,0,8d01
  //   ,8201,9104,0,8e04,7,a00f
  //   break instruction
  //   data word instruction
  //   jump instruction
  //   ALU instruction
endmodule

/* Test case increment forever:
startClock programClock instructionPointer A B mAx

program(0x0000, 0x8A02, 0x8201, 0xA001)

1 0  0x0000  X       X       X
0 C  0x0001  0x0000  X       X
0 C  0x0002  0x0000  0x0002  0x0000
0 C  0x0003  0x0001  0x0002  0x0000
0 C  0x0002  0x0001  0x0002  0x0000
0 C  0x0003  0x0002  0x0002  0x0000
0 C  0x0002  0x0002  0x0002  0x0000
0 C  0x0003  0x0003  0x0002  0x0000
0 C  0x0002  0x0003  0x0002  0x0000
0 C  0x0003  0x0004  0x0002  0x0000
0 C  0x0002  0x0004  0x0002  0x0000
0 C  0x0003  0x0005  0x0002  0x0000
0 C  0x0002  0x0005  0x0002  0x0000
0 C  0x0003  0x0006  0x0002  0x0000
*/

/* Test case fill ram cells with address:
startClock programClock instructionPointer instruction At mAt

program(0x8502, 0xD104, 0x9202, 0x0001, 0xA00F)

1 0 0x0000  0x8502  0       X

loop(i, 16)
1 C 0x0001  0xD104  0       X
1 C 0x0002  0x9202  0       X
1 C 0x0003  0x0001  0       X
1 C 0x0004  0xA00F  0       X
end loop

loop(j, 16)
1 0 X  X  (j)  (j)
end loop
*/

/* Test case compute fibonacci:
startClock programClock testRamClock At mAt

program(0x0001, 0x8904, 0x8201, 0x8904, 0x8102, 0x0000, 0x9104, 0x0000, 0x8D01, 0x8D02, 0x8209, 0x8D01, 0x8002, 0x0000, 0x8D01, 0x8201, 0x9104, 0x0000, 0x8E04, 0x0007, 0xA00F)

1 0 0 0 0

# Compute 20 fibonacci numbers (cycle count is not perfect)
loop(i, 280)
0 C 0 0 X
end loop

0 0 0 0 X

0 0 C  0  0x0015
0 0 C  1  0x0001
0 0 C  2  0x0001
0 0 C  3  0x0002
0 0 C  4  0x0003
0 0 C  5  0x0005
0 0 C  6  0x0008
0 0 C  7  0x000D
0 0 C  8  0x0015
0 0 C  9  0x0022
0 0 C 10  0x0037
0 0 C 11  0x0059
0 0 C 12  0x0090
0 0 C 13  0x00E9
0 0 C 14  0x0179
0 0 C 15  0x0262
0 0 C 16  0x03DB
0 0 C 17  0x063D
0 0 C 18  0x0A18
0 0 C 19  0x1055
0 0 C 20  0x1A6D
0 0 C 21  0x2AC2
*/
