// Digital circuit computer_proc16a2.dig as structural Verilog
module computer_proc16a2 (
  input  programClock,
  input  stopClock,
  input  startClock,
  input  [15:0] At_2,
  output [15:0] At
);

  wire and_1_out, cpu_proc16a2_1_p4, cpu_proc16a2_1_p5, cpu_proc16a2_1_p8, cpu_proc16a2_1_p9,
       cpu_proc16a2_1_p10, or_1_out, or_2_out, or_3_out, reset_PC_out, rs_ff_as_1_q, step_out;
  wire [15:0] counterpreset_1_out, cpu_proc16a2_1_p6, cpu_proc16a2_1_p7, ramdualaccess_1_d1, rom_1_d;

  or or_1 (or_1_out, stopClock, cpu_proc16a2_1_p8);
  Break break_1 (.brk(cpu_proc16a2_1_p8));
  RS_FF_AS rs_ff_as_1 (.S(startClock), .R(or_1_out), .Q(rs_ff_as_1_q));  // open: nQ
  and and_1 (and_1_out, programClock, rs_ff_as_1_q);
  or or_2 (or_2_out, step_out, reset_PC_out);
  Button step (.out(step_out));
  Button reset_PC (.out(reset_PC_out));
  or or_3 (or_3_out, and_1_out, or_2_out);
  CounterPreset #(.Bits(16), .isProgramCounter("true")) counterpreset_1 (
    .en(1'b1), .C(or_3_out), .dir(1'b0), .in(cpu_proc16a2_1_p7), .ld(cpu_proc16a2_1_p4), .clr(reset_PC_out),
    .out(counterpreset_1_out));  // open: ovf
  RAMDualAccess #(.AddrBits(16), .Bits(16)) ramdualaccess_1 (
    .str(cpu_proc16a2_1_p5), .C(or_3_out), .ld(1'b1), .A1(cpu_proc16a2_1_p6), .Din1(cpu_proc16a2_1_p7),
    .A2(At_2), .D1(ramdualaccess_1_d1), .D2(At));
  // Probe PC on counterpreset_1_out
  ROM #(.AddrBits(16), .isProgramMemory("true"), .Bits(16)) rom_1 (.A(counterpreset_1_out), .sel(1'b1), .D(rom_1_d));
  // cpu_proc16a2 cpu_proc16a2_1: pin names not known; wires that end beside it: or_3_out, ramdualaccess_1_d1, rom_1_d, cpu_proc16a2_1_p4, cpu_proc16a2_1_p5, cpu_proc16a2_1_p6, cpu_proc16a2_1_p7, cpu_proc16a2_1_p8, cpu_proc16a2_1_p9, cpu_proc16a2_1_p10
  // Probe I on rom_1_d
  // Probe test_B on cpu_proc16a2_1_p9
  // Probe on cpu_proc16a2_1_p9
  // Probe on cpu_proc16a2_1_p9
  // Probe test_A on cpu_proc16a2_1_p10
  // Probe on cpu_proc16a2_1_p10
  // Probe on cpu_proc16a2_1_p10

  // Notes on the sheet:
  //   Clock
  //   contents of rom_1 (hex, n*v repeats v):
  //   1,8904,8201,8904,8102,0,9104,0,8d01,8d02,8209,8d01,8002,0,8d01
  //   ,8201,9104,0,8e04,7,a00f
endmodule

/* Test case increment forever:
startClock programClock PC test_A test_B

program(0x0000, 0x8A02, 0x8201, 0xA001)

1 0  0x0000  X       X
0 C  0x0001  0x0000  X
0 C  0x0002  0x0000  0x0002
0 C  0x0003  0x0001  0x0002
0 C  0x0002  0x0001  0x0002
0 C  0x0003  0x0002  0x0002
0 C  0x0002  0x0002  0x0002
0 C  0x0003  0x0003  0x0002
0 C  0x0002  0x0003  0x0002
0 C  0x0003  0x0004  0x0002
0 C  0x0002  0x0004  0x0002
0 C  0x0003  0x0005  0x0002
0 C  0x0002  0x0005  0x0002
0 C  0x0003  0x0006  0x0002
*/

/* Test case fill ram cells with address:
startClock programClock PC I At *At

program(0x8502, 0xD104, 0x9202, 0x0001, 0xA00F)

1 0 0x0000  0x8502  0       X

loop(i, 16)
1 C 0x0001  0xD104  0       X
1 C 0x0002  0x9202  0       X
1 C 0x0003  0x0001  0       X
1 C 0x0004  0xA00F  0       X
end loop

loop(j, 16)
1 0 X  X  (j)  (j)
end loop
*/

/* Test case compute fibonacci:
startClock programClock At *At PC

program(0x0001, 0x8904, 0x8201, 0x8904, 0x8102, 0x0000, 0x9104, 0x0000, 0x8D01, 0x8D02, 0x8209, 0x8D01, 0x8002, 0x0000, 0x8D01, 0x8201, 0x9104, 0x0000, 0x8E04, 0x0007, 0xA00F)

1 0 0 0 x

loop(i, 6)
  0 C 0xFFFF 0 x
end loop

0 C 0x0000 2 7


loop(j, 11)
  0 C 0xFFFF 0 x
end loop

0 C 0 3 19
0 C 3 2 20



loop(j, 12)
  0 C 0xFFFF 0 x
end loop

0 C 0 4 x
0 C 4 3 x



loop(j, 12)
  0 C 0xFFFF 0 x
end loop

0 C 0 5 x
0 C 5 5 x
######


loop(j, 12)
  0 C 0xFFFF 0 x
end loop

0 C 0 6 x
0 C 6 8 x



loop(j, 12)
  0 C 0xFFFF 0 x
end loop

0 C 0 7 x
0 C 7 13 x



loop(j, 12)
  0 C 0xFFFF 0 x
end loop

0 C 0 8 x
0 C 8 21 x



loop(j, 12)
  0 C 0xFFFF 0 x
end loop

0 C 0 9 x
0 C 9 34 x



loop(j, 12)
  0 C 0xFFFF 0 x
end loop

0 C 0 10 x
0 C 10 55 x



loop(j, 12)
  0 C 0xFFFF 0 x
end loop

0 C 0 11 x
0 C 11 89 x



loop(j, 12)
  0 C 0xFFFF 0 x
end loop

0 C 0 12 x
0 C 12 144 x



loop(j, 12)
  0 C 0xFFFF 0 x
end loop

0 C 0 13 x
0 C 13 233 x



loop(j, 12)
  0 C 0xFFFF 0 x
end loop

0 C 0 14 x
0 C 14 377 x



loop(j, 12)
  0 C 0xFFFF 0 x
end loop

0 C 0 15 x
0 C 15 610 x



loop(j, 12)
  0 C 0xFFFF 0 x
end loop

0 C 0 16 x
0 C 16 987 x
*/
