// Digital circuit computer_proc16a2_mappedmemory.dig as structural Verilog
module computer_proc16a2_mappedmemory (
  input  programClock,
  input  stopClock,
  input  startClock,
  input  [13:0] At_2,
  input  color_mode,
  output [15:0] At
);

  wire and_1_out, and_2_out, and_3_out, or_1_out, or_2_out, or_3_out, proc16a2_1_brk, proc16a2_1_pcw,
       proc16a2_1_rw, reset_PC_out, rs_ff_as_1_q, step_out;
  wire [3:0] demultiplexer_2_out_1;
  wire [7:0] button_device;
  wire [8:0] demultiplexer_2_out_1_2;
  wire [12:0] demultiplexer_2_out_0;
  wire [13:0] demultiplexer_1_out_0;
  wire [15:0] counterpreset_1_out, multiplexer_1_out, multiplexer_2_out, proc16a2_1_a_2, proc16a2_1_r,
       proc16a2_1_test_a, proc16a2_1_test_b, ramdualaccess_1_d1, rom_1_d;

  or or_1 (or_1_out, stopClock, proc16a2_1_brk);
  Break break_1 (.brk(proc16a2_1_brk));
  RS_FF_AS rs_ff_as_1 (.S(startClock), .R(or_1_out), .Q(rs_ff_as_1_q));  // open: nQ
  and and_1 (and_1_out, programClock, rs_ff_as_1_q);
  or or_2 (or_2_out, step_out, reset_PC_out);
  Button step (.out(step_out));
  Button reset_PC (.out(reset_PC_out));
  or or_3 (or_3_out, and_1_out, or_2_out);
  Demultiplexer #(.Bits(14)) demultiplexer_1 (
    .sel(proc16a2_1_a_2[14]), .in(proc16a2_1_a_2[13:0]), .out_0(demultiplexer_1_out_0));  // open: out_1
  Demultiplexer #(.Bits(13)) demultiplexer_2 (
    .sel(1'b0), .in({13{1'b0}}), .out_0(demultiplexer_2_out_0),
    .out_1({demultiplexer_2_out_1_2, demultiplexer_2_out_1}));
  Demultiplexer #(.Bits(16), .Selector_Bits(4)) demultiplexer_3 (
    .sel(demultiplexer_2_out_1), .in({16{1'b0}}));  // open: out_0, out_1, out_2, out_3, out_4, out_5, out_6, out_7, out_8, out_9, out_10, out_11, out_12, out_13, out_14, out_15
  and and_2 (and_2_out, proc16a2_1_rw, ~proc16a2_1_a_2[14]);  // And
  and and_3 (and_3_out, 1'b0, 1'b0);
  CounterPreset #(.Bits(16), .isProgramCounter("true")) counterpreset_1 (
    .en(1'b1), .C(or_3_out), .dir(1'b0), .in(proc16a2_1_r), .ld(proc16a2_1_pcw), .clr(reset_PC_out),
    .out(counterpreset_1_out));  // open: ovf
  RAMDualAccess #(.AddrBits(14), .Bits(16)) ramdualaccess_1 (
    .str(and_2_out), .C(or_3_out), .ld(1'b1), .A1(demultiplexer_1_out_0), .Din1(proc16a2_1_r), .A2(At_2),
    .D1(ramdualaccess_1_d1), .D2(At));
  GraphicCard #(.graphicHeight(64), .graphicWidth(64), .Bits(16)) graphiccard_1 (
    .A(demultiplexer_2_out_0), .str(and_3_out), .C(1'b0), .ld(1'b1), .B(color_mode), .D({16{1'b0}}));
  // Probe PC on counterpreset_1_out
  ROM #(.AddrBits(16), .isProgramMemory("true"), .Bits(16)) rom_1 (.A(counterpreset_1_out), .sel(1'b1), .D(rom_1_d));
  Multiplexer #(.Bits(16)) multiplexer_1 (
    .sel(proc16a2_1_a_2[14]), .in_0(ramdualaccess_1_d1), .in_1({16{1'b0}}), .out(multiplexer_1_out));
  Multiplexer #(.Bits(16)) multiplexer_2 (
    .sel(1'b0), .in_0({16{1'b0}}), .in_1({{8{1'b0}}, button_device}), .out(multiplexer_2_out));
  proc16a2 proc16a2_1 (
    .C(or_3_out), .A(multiplexer_1_out), .PC(rom_1_d), .pcw(proc16a2_1_pcw), .rw(proc16a2_1_rw),
    .A_2(proc16a2_1_a_2), .R(proc16a2_1_r), .brk(proc16a2_1_brk), .test_B(proc16a2_1_test_b),
    .test_A(proc16a2_1_test_a));
  // Probe I on rom_1_d
  // Probe test_B on proc16a2_1_test_b
  // Probe on proc16a2_1_test_b
  // Probe on proc16a2_1_test_b
  // Probe test_A on proc16a2_1_test_a
  // Probe on proc16a2_1_test_a
  // Probe on proc16a2_1_test_a
  Button LEFT (.out(button_device[5]));
  Button UP (.out(button_device[7]));
  Button DOWN (.out(button_device[6]));
  Button RIGHT (.out(button_device[4]));
  // Probe A on proc16a2_1_a_2
  // Probe on proc16a2_1_a_2
  // Probe on proc16a2_1_a_2
  // Probe R on proc16a2_1_r
  // Probe on proc16a2_1_r
  // Probe on proc16a2_1_r
  Button B (.out(button_device[2]));
  Button A_2 (.out(button_device[3]));
  Button Y (.out(button_device[0]));
  Button X (.out(button_device[1]));
  // also tied to GND on the sheet: {demultiplexer_2_out_1[0], demultiplexer_2_out_1[1], demultiplexer_2_out_1[2], demultiplexer_2_out_1[3], demultiplexer_2_out_1_2[0], demultiplexer_2_out_1_2[1], demultiplexer_2_out_1_2[2], demultiplexer_2_out_1_2[3], demultiplexer_2_out_1_2[4], demultiplexer_2_out_1_2[5], demultiplexer_2_out_1_2[6], demultiplexer_2_out_1_2[7], demultiplexer_2_out_1_2[8], multiplexer_2_out[0], multiplexer_2_out[1], multiplexer_2_out[2], multiplexer_2_out[3], multiplexer_2_out[4], multiplexer_2_out[5], multiplexer_2_out[6], multiplexer_2_out[7], multiplexer_2_out[8], multiplexer_2_out[9], multiplexer_2_out[10], multiplexer_2_out[11], multiplexer_2_out[12], multiplexer_2_out[13], multiplexer_2_out[14], multiplexer_2_out[15]}

  // Notes on the sheet:
  //   Clock
  //   Address map:
  //   0x0000 - 0x3FFF (16Ki) RAM
  //   0x4000 - 0xBFFF (8Ki) video memory
  //   0xC000 - 0xC00F (16) devices
  //   0xC010 - 0xFFFF unusable
  //   devices:
  //   0x4000: button inputs
  //   RAM
  //   VRAM
  //   devices
  //   contents of rom_1 (hex, n*v repeats v):
  //   1,8904,8201,8904,8102,0,9104,0,8d01,8d02,8209,8d01,8002,0,8d01
  //   ,8201,9104,0,8e04,7,a00f
  //   button device
  //   bits 15-8 are unconnected
  //   7 6543210
  //   UDLRABXY
endmodule

/* Test case increment forever:
startClock programClock PC test_A test_B

program(0x0000, 0x8A02, 0x8201, 0xA001)

1 0  0x0000  X       X
0 C  0x0001  0x0000  X
0 C  0x0002  0x0000  0x0002
0 C  0x0003  0x0001  0x0002
0 C  0x0002  0x0001  0x0002
0 C  0x0003  0x0002  0x0002
0 C  0x0002  0x0002  0x0002
0 C  0x0003  0x0003  0x0002
0 C  0x0002  0x0003  0x0002
0 C  0x0003  0x0004  0x0002
0 C  0x0002  0x0004  0x0002
0 C  0x0003  0x0005  0x0002
0 C  0x0002  0x0005  0x0002
0 C  0x0003  0x0006  0x0002
*/

/* Test case fill ram cells with address:
startClock programClock PC I At *At

program(0x8502, 0xD104, 0x9202, 0x0001, 0xA00F)

1 0 0x0000  0x8502  0       X

loop(i, 16)
1 C 0x0001  0xD104  0       X
1 C 0x0002  0x9202  0       X
1 C 0x0003  0x0001  0       X
1 C 0x0004  0xA00F  0       X
end loop

loop(j, 16)
1 0 X  X  (j)  (j)
end loop
*/

/* Test case compute fibonacci:
startClock programClock At *At PC

program(0x0001, 0x8904, 0x8201, 0x8904, 0x8102, 0x0000, 0x9104, 0x0000, 0x8D01, 0x8D02, 0x8209, 0x8D01, 0x8002, 0x0000, 0x8D01, 0x8201, 0x9104, 0x0000, 0x8E04, 0x0007, 0xA00F)

1 0 0 0 x

loop(i, 6)
  0 C 0xFFFF 0 x
end loop

0 C 0x0000 2 7


loop(j, 11)
  0 C 0xFFFF 0 x
end loop

0 C 0 3 19
0 C 3 2 20



loop(j, 12)
  0 C 0xFFFF 0 x
end loop

0 C 0 4 x
0 C 4 3 x



loop(j, 12)
  0 C 0xFFFF 0 x
end loop

0 C 0 5 x
0 C 5 5 x
######


loop(j, 12)
  0 C 0xFFFF 0 x
end loop

0 C 0 6 x
0 C 6 8 x



loop(j, 12)
  0 C 0xFFFF 0 x
end loop

0 C 0 7 x
0 C 7 13 x



loop(j, 12)
  0 C 0xFFFF 0 x
end loop

0 C 0 8 x
0 C 8 21 x



loop(j, 12)
  0 C 0xFFFF 0 x
end loop

0 C 0 9 x
0 C 9 34 x



loop(j, 12)
  0 C 0xFFFF 0 x
end loop

0 C 0 10 x
0 C 10 55 x



loop(j, 12)
  0 C 0xFFFF 0 x
end loop

0 C 0 11 x
0 C 11 89 x



loop(j, 12)
  0 C 0xFFFF 0 x
end loop

0 C 0 12 x
0 C 12 144 x



loop(j, 12)
  0 C 0xFFFF 0 x
end loop

0 C 0 13 x
0 C 13 233 x



loop(j, 12)
  0 C 0xFFFF 0 x
end loop

0 C 0 14 x
0 C 14 377 x



loop(j, 12)
  0 C 0xFFFF 0 x
end loop

0 C 0 15 x
0 C 15 610 x



loop(j, 12)
  0 C 0xFFFF 0 x
end loop

0 C 0 16 x
0 C 16 987 x
*/
