// Digital circuit eq0.dig as structural Verilog
module eq0 (
  input  [15:0] a,
  output x
);

  nor nor_1 (x, a[0], a[1], a[2], a[3], a[4], a[5], a[6], a[7], a[8], a[9], a[10], a[11], a[12], a[13], a[14], a[15]);
endmodule

/* Test case:
a    x
0    1
1    0
2    0
3    0
4    0
*/
