// Digital circuit inc16.dig as structural Verilog
module inc16 (
  input  [15:0] a,
  output [15:0] x
);

  wire not_1_out;

  Add #(.Bits(16)) add_1 (.a(a), .b({16{1'b0}}), .c_i(not_1_out), .s(x));  // open: c_o
  not not_1 (not_1_out, 1'b0);
endmodule

/* Test case:
a   x
0   1
1   2
3   4
15  16
16  17
*/
