// Digital circuit isneg16.dig as structural Verilog
module isneg16 (
  input  [15:0] a,
  output is_neg
);


  assign is_neg = a[15];
endmodule

/* Test case:
a  is_neg
0  0
1  0
2  0
0x7fff 0
0x8000 1
0xffff 1
*/
