// Digital circuit jump16_1.dig as structural Verilog
module jump16_1 (
  input  [15:0] A,
  input  [15:0] B,
  input  [10:0] I,
  output j,
  output [15:0] Ai
);

  wire [15:0] multiplexer_1_out;

  Multiplexer #(.Bits(16)) multiplexer_1 (.sel(I[3]), .in_0(A), .in_1(B), .out(multiplexer_1_out));
  compare16_1 compare16_1_1 (.A(multiplexer_1_out), .B({16{1'b0}}), .m(I[2:0]), .r(j));
  Multiplexer #(.Bits(16)) multiplexer_2 (.sel(I[3]), .in_0(B), .in_1(A), .out(Ai));
endmodule

/* Test case jump tests:
A       B       I       j Ai
0x0000  0x0000  0b0000  0 X
0x0001  0x0000  0b0000  0 X
0x0002  0x0000  0b0000  0 X
0x0000  0x0001  0b0000  0 X
0x0001  0x0001  0b0000  0 X
0x0002  0x0001  0b0000  0 X
0x0000  0x0002  0b0000  0 X
0x0001  0x0002  0b0000  0 X
0x0002  0x0002  0b0000  0 X
0xFFFF  0x0003  0b0000  0 X

0x0000  0x0000  0b0001  0 X
0x0001  0x0000  0b0001  1 0x0000
0x0002  0x0000  0b0001  1 0x0000
0x0000  0x0001  0b0001  0 X
0x0001  0x0001  0b0001  1 0x0001
0x0002  0x0001  0b0001  1 0x0001
0x0000  0x0002  0b0001  0 X
0x0001  0x0002  0b0001  1 0x0002
0x0002  0x0002  0b0001  1 0x0002
0xFFFF  0x0003  0b0001  0 X

0x0000  0x0000  0b0010  1 0x0000
0x0001  0x0000  0b0010  0 X
0x0002  0x0000  0b0010  0 X
0x0000  0x0001  0b0010  1 0x0001
0x0001  0x0001  0b0010  0 X
0x0002  0x0001  0b0010  0 X
0x0000  0x0002  0b0010  1 0x0002
0x0001  0x0002  0b0010  0 X
0x0002  0x0002  0b0010  0 X
0xFFFF  0x0003  0b0010  0 X

0x0000  0x0000  0b0011  1 0x0000
0x0001  0x0000  0b0011  1 0x0000
0x0002  0x0000  0b0011  1 0x0000
0x0000  0x0001  0b0011  1 0x0001
0x0001  0x0001  0b0011  1 0x0001
0x0002  0x0001  0b0011  1 0x0001
0x0000  0x0002  0b0011  1 0x0002
0x0001  0x0002  0b0011  1 0x0002
0x0002  0x0002  0b0011  1 0x0002
0xFFFF  0x0003  0b0011  0 X

0x0000  0x0005  0b0100  0 X
0x0001  0x0005  0b0100  0 X
0xFFFF  0x0005  0b0100  1 0x0005

0x0000  0x0005  0b0101  0 X
0x0001  0x0005  0b0101  1 0x0005
0xFFFF  0x0005  0b0101  1 0x0005

0x0000  0x0005  0b0110  1 0x0005
0x0001  0x0005  0b0110  0 X
0xFFFF  0x0005  0b0110  1 0x0005

0x0000  0x0005  0b0111  1 0x0005
0x0001  0x0005  0b0111  1 0x0005
0xFFFF  0x0005  0b0111  1 0x0005


0x0005  0x0000  0b1100  0 X
0x0005  0x0001  0b1100  0 X
0x0005  0xFFFF  0b1100  1 0x0005

0x0005  0x0000  0b1101  0 X
0x0005  0x0001  0b1101  1 0x0005
0x0005  0xFFFF  0b1101  1 0x0005

0x0005  0x0000  0b1110  1 0x0005
0x0005  0x0001  0b1110  0 X
0x0005  0xFFFF  0b1110  1 0x0005

0x0005  0x0000  0b1111  1 0x0005
0x0005  0x0001  0b1111  1 0x0005
0x0005  0xFFFF  0b1111  1 0x0005
*/
