// Digital circuit jump16_2.dig as structural Verilog
module jump16_2 (
  input  [15:0] A,
  input  [15:0] B,
  input  [2:0] mode,
  input  sel,
  output j,
  output [15:0] Ai
);

  wire [15:0] multiplexer_1_out;

  Multiplexer #(.Bits(16)) multiplexer_1 (.sel(sel), .in_0(A), .in_1(B), .out(multiplexer_1_out));
  compare16_1 compare16_1_1 (.A(multiplexer_1_out), .B({16{1'b0}}), .m(mode), .r(j));
  Multiplexer #(.Bits(16)) multiplexer_2 (.sel(sel), .in_0(B), .in_1(A), .out(Ai));
endmodule

/* Test case jump tests:
A       B       mode  sel j Ai
0x0000  0x0000  0b000 0   0 X
0x0001  0x0000  0b000 0   0 X
0x0002  0x0000  0b000 0   0 X
0x0000  0x0001  0b000 0   0 X
0x0001  0x0001  0b000 0   0 X
0x0002  0x0001  0b000 0   0 X
0x0000  0x0002  0b000 0   0 X
0x0001  0x0002  0b000 0   0 X
0x0002  0x0002  0b000 0   0 X
0xFFFF  0x0003  0b000 0   0 X

0x0000  0x0000  0b001 0   0 X
0x0001  0x0000  0b001 0   1 0x0000
0x0002  0x0000  0b001 0   1 0x0000
0x0000  0x0001  0b001 0   0 X
0x0001  0x0001  0b001 0   1 0x0001
0x0002  0x0001  0b001 0   1 0x0001
0x0000  0x0002  0b001 0   0 X
0x0001  0x0002  0b001 0   1 0x0002
0x0002  0x0002  0b001 0   1 0x0002
0xFFFF  0x0003  0b001 0   0 X

0x0000  0x0000  0b010 0   1 0x0000
0x0001  0x0000  0b010 0   0 X
0x0002  0x0000  0b010 0   0 X
0x0000  0x0001  0b010 0   1 0x0001
0x0001  0x0001  0b010 0   0 X
0x0002  0x0001  0b010 0   0 X
0x0000  0x0002  0b010 0   1 0x0002
0x0001  0x0002  0b010 0   0 X
0x0002  0x0002  0b010 0   0 X
0xFFFF  0x0003  0b010 0   0 X

0x0000  0x0000  0b011 0   1 0x0000
0x0001  0x0000  0b011 0   1 0x0000
0x0002  0x0000  0b011 0   1 0x0000
0x0000  0x0001  0b011 0   1 0x0001
0x0001  0x0001  0b011 0   1 0x0001
0x0002  0x0001  0b011 0   1 0x0001
0x0000  0x0002  0b011 0   1 0x0002
0x0001  0x0002  0b011 0   1 0x0002
0x0002  0x0002  0b011 0   1 0x0002
0xFFFF  0x0003  0b011 0   0 X

0x0000  0x0005  0b100 0   0 X
0x0001  0x0005  0b100 0   0 X
0xFFFF  0x0005  0b100 0   1 0x0005

0x0000  0x0005  0b101 0   0 X
0x0001  0x0005  0b101 0   1 0x0005
0xFFFF  0x0005  0b101 0   1 0x0005

0x0000  0x0005  0b110 0   1 0x0005
0x0001  0x0005  0b110 0   0 X
0xFFFF  0x0005  0b110 0   1 0x0005

0x0000  0x0005  0b111 0   1 0x0005
0x0001  0x0005  0b111 0   1 0x0005
0xFFFF  0x0005  0b111 0   1 0x0005


0x0005  0x0000  0b100 1   0 X
0x0005  0x0001  0b100 1   0 X
0x0005  0xFFFF  0b100 1   1 0x0005

0x0005  0x0000  0b101 1   0 X
0x0005  0x0001  0b101 1   1 0x0005
0x0005  0xFFFF  0b101 1   1 0x0005

0x0005  0x0000  0b110 1   1 0x0005
0x0005  0x0001  0b110 1   0 X
0x0005  0xFFFF  0b110 1   1 0x0005

0x0005  0x0000  0b111 1   1 0x0005
0x0005  0x0001  0b111 1   1 0x0005
0x0005  0xFFFF  0b111 1   1 0x0005
*/
