// Digital circuit latch1.dig as structural Verilog
module latch1 (
  input  st,
  input  d,
  output x
);

  Multiplexer multiplexer_1 (.sel(st), .in_0(x), .in_1(d), .out(x));
endmodule

/* Test case latch test:
st d  x
C  0  0
0  0  0
0  1  0
0  0  0
1  0  0
0  0  0
1  0  0
1  1  1
1  0  0
0  0  0

1  0  0
1  1  1
0  1  1
0  0  1
0  1  1
0  0  1
1  0  0
0  0  0
0  1  0
1  1  1
1  0  0
0  0  0
*/
