// Digital circuit latch16.dig as structural Verilog
module latch16 (
  input  st,
  input  [15:0] d,
  output [15:0] x
);

  Multiplexer #(.Bits(16)) multiplexer_1 (.sel(st), .in_0(x), .in_1(d), .out(x));
endmodule

/* Test case latch test:
st d  x
0  0  0
0  1  0
0  0  0
1  0  0
0  0  0
1  0  0
1  1  1
1  0  0
0  0  0

1  0  0
1  1  1
0  1  1
0  0  1
0  1  1
0  0  1
1  0  0
0  0  0
0  1  0
1  1  1
1  0  0
0  0  0



0  0  0
0  13 0
0  0  0
1  0  0
0  0  0
1  0  0
1  13 13
1  0  0
0  0  0

1  0  0
1  13 13
0  13 13
0  0  13
0  13 13
0  0  13
1  0  0
0  0  0
0  13 0
1  13 13
1  0  0
0  0  0
*/
