// Digital circuit proc16a1.dig as structural Verilog
module proc16a1 (
  input  programClock
);

  wire and_1_out, jump16_1_1_j, not_1_out, or_1_out, or_2_out, or_3_out, or_4_out, reset_PC_out,
       rs_ff_as_1_q, start_clock_out, step_out, stop_clock_out;
  wire [10:0] demultiplexer_3_out_0, demultiplexer_3_out_1;
  wire [12:0] demultiplexer_2_out_0, demultiplexer_2_out_1;
  wire [14:0] demultiplexer_1_out_0, demultiplexer_1_out_1;
  wire [15:0] ALU_r, jump16_1_1_ai, multiplexer_1_out, multiplexer_2_out, programCounter_out, R_A_q, R_B_q,
       RAM_d, rom_1_d;

  Break break_simulation (.brk(demultiplexer_3_out_1[0]));
  RS_FF_AS rs_ff_as_1 (.S(start_clock_out), .R(or_1_out), .Q(rs_ff_as_1_q));  // open: nQ
  Button start_clock (.out(start_clock_out));
  Button stop_clock (.out(stop_clock_out));
  or or_1 (or_1_out, stop_clock_out, demultiplexer_3_out_1[0]);
  and and_1 (and_1_out, programClock, rs_ff_as_1_q);
  Button step (.out(step_out));
  Button reset_PC (.out(reset_PC_out));
  or or_2 (or_2_out, and_1_out, or_3_out);
  or or_3 (or_3_out, step_out, reset_PC_out);
  CounterPreset #(.Bits(16), .isProgramCounter("true")) programCounter (
    .en(1'b1), .C(or_2_out), .dir(1'b0), .in(jump16_1_1_ai), .ld(jump16_1_1_j), .clr(reset_PC_out),
    .out(programCounter_out));  // open: ovf
  Register #(.Bits(16)) R_A (.D(multiplexer_2_out), .C(or_2_out), .en(or_4_out), .Q(R_A_q));
  Register #(.Bits(16)) R_B (.D(multiplexer_2_out), .C(or_2_out), .en(demultiplexer_2_out_0[1]), .Q(R_B_q));
  RAMDualPort #(.AddrBits(16), .Bits(16)) RAM (
    .A(multiplexer_1_out), .Din(multiplexer_2_out), .str(demultiplexer_2_out_0[2]), .C(or_2_out), .ld(1'b1),
    .D(RAM_d));
  // Probe instructionPointer on programCounter_out
  ROM #(.AddrBits(16), .isProgramMemory("true"), .Bits(16)) rom_1 (.A(programCounter_out), .sel(1'b1), .D(rom_1_d));
  Multiplexer #(.Bits(16)) multiplexer_1 (
    .sel(demultiplexer_1_out_1[14]), .in_0(R_A_q), .in_1(R_B_q), .out(multiplexer_1_out));
  // Probe Ax on multiplexer_1_out
  // Probe A on R_A_q
  // Probe instruction on rom_1_d
  // Probe B on R_B_q
  Demultiplexer #(.Bits(15)) demultiplexer_1 (
    .sel(rom_1_d[15]), .in(rom_1_d[14:0]), .out_0(demultiplexer_1_out_0), .out_1(demultiplexer_1_out_1));
  // Probe mAx on RAM_d
  or or_4 (or_4_out, demultiplexer_2_out_0[0], not_1_out);
  not not_1 (not_1_out, rom_1_d[15]);
  Demultiplexer #(.Bits(13)) demultiplexer_2 (
    .sel(demultiplexer_1_out_1[13]), .in(demultiplexer_1_out_1[12:0]), .out_0(demultiplexer_2_out_0),
    .out_1(demultiplexer_2_out_1));
  Demultiplexer #(.Bits(11)) demultiplexer_3 (
    .sel(demultiplexer_2_out_1[11]), .in(demultiplexer_2_out_1[10:0]), .out_0(demultiplexer_3_out_0),
    .out_1(demultiplexer_3_out_1));
  alu16_2 ALU (.opcode(demultiplexer_2_out_0), .A(R_A_q), .B(R_B_q), .Ax(RAM_d), .R(ALU_r));
  jump16_1 jump16_1_1 (.A(R_A_q), .B(R_B_q), .I(demultiplexer_3_out_0), .j(jump16_1_1_j), .Ai(jump16_1_1_ai));
  Multiplexer #(.Bits(16)) multiplexer_2 (
    .sel(rom_1_d[15]), .in_0({1'b0, demultiplexer_1_out_0}), .in_1(ALU_r), .out(multiplexer_2_out));
  // Probe output on multiplexer_2_out
  // also tied to GND on the sheet: demultiplexer_2_out_1[12]

  // Notes on the sheet:
  //   Clock
  //   contents of rom_1 (hex, n*v repeats v):
  //   8502,d104,9202,1,900f
  //   break instruction
  //   data word instruction
  //   jump instruction
  //   ALU instruction
endmodule

/* Test case increment forever:
programClock instructionPointer instruction A B mAx

program(0x0000, 0x8A02, 0x8201, 0x9001)

0  0x0000  0x0000  X       X       0x0000
C  0x0001  0x8A02  0x0000  X       0x0000
C  0x0002  0x8201  0x0000  0x0002  0x0000
C  0x0003  0x9001  0x0001  0x0002  0x0000
C  0x0002  0x8201  0x0001  0x0002  0x0000
C  0x0003  0x9001  0x0002  0x0002  0x0000
C  0x0002  0x8201  0x0002  0x0002  0x0000
C  0x0003  0x9001  0x0003  0x0002  0x0000
C  0x0002  0x8201  0x0003  0x0002  0x0000
C  0x0003  0x9001  0x0004  0x0002  0x0000
C  0x0002  0x8201  0x0004  0x0002  0x0000
C  0x0003  0x9001  0x0005  0x0002  0x0000
C  0x0002  0x8201  0x0005  0x0002  0x0000
C  0x0003  0x9001  0x0006  0x0002  0x0000
*/
