// Digital circuit proc16a2.dig as structural Verilog
module proc16a2 (
  input  C,
  input  [15:0] A,
  input  [15:0] PC,
  output pcw,
  output rw,
  output [15:0] A_2,
  output [15:0] R,
  output brk,
  output [15:0] test_B,
  output [15:0] test_A
);

  wire decode16a1_1_a, decode16a1_1_alu_rsel, decode16a1_1_ax_sel, decode16a1_1_b, decode16a1_1_cmp_o;
  wire [1:0] decode16a1_1_alu_a, decode16a1_1_alu_b, decode16a1_1_d_sel;
  wire [2:0] decode16a1_1_cmp;
  wire [4:0] decode16a1_1_alu;
  wire [15:0] alu16_2_1_r, alu16_2_operands_1_x, alu16_2_operands_1_y, jump16_2_1_ai, multiplexer_2_out;

  // Probe on PC
  // Probe on PC
  // Probe on PC
  // Probe on A
  // Probe on A
  // Probe on A
  Register #(.Bits(16)) rA (.D(multiplexer_2_out), .C(C), .en(decode16a1_1_a), .Q(test_A));
  Register #(.Bits(16)) rB (.D(multiplexer_2_out), .C(C), .en(decode16a1_1_b), .Q(test_B));
  decode16a1 decode16a1_1 (
    .I(PC), .ALU(decode16a1_1_alu), .ALU_A(decode16a1_1_alu_a), .ALU_B(decode16a1_1_alu_b),
    .D_sel(decode16a1_1_d_sel), .Ax(rw), .B(decode16a1_1_b), .A(decode16a1_1_a), .cmp(decode16a1_1_cmp),
    .brk(brk), .cmp_o(decode16a1_1_cmp_o), .Ax_sel(decode16a1_1_ax_sel), .ALU_rsel(decode16a1_1_alu_rsel));  // open: jmp
  // Probe on test_A
  // Probe on test_A
  // Probe on test_A
  // Probe on test_B
  // Probe on test_B
  // Probe on test_B
  alu16_2_operands alu16_2_operands_1 (
    .A(test_A), .B(test_B), .Ax(A), .Rsel(decode16a1_1_alu_rsel), .Xsel(decode16a1_1_alu_a),
    .Ysel(decode16a1_1_alu_b), .X(alu16_2_operands_1_x), .Y(alu16_2_operands_1_y));
  alu16_2 alu16_2_1 (.opcode(decode16a1_1_alu), .X(alu16_2_operands_1_x), .Y(alu16_2_operands_1_y), .R(alu16_2_1_r));
  // Probe on alu16_2_1_r
  // Probe on alu16_2_1_r
  // Probe on alu16_2_1_r
  Multiplexer #(.Bits(16)) multiplexer_1 (.sel(decode16a1_1_ax_sel), .in_0(test_A), .in_1(test_B), .out(A_2));
  jump16_2 jump16_2_1 (
    .A(test_A), .B(test_B), .mode(decode16a1_1_cmp), .sel(decode16a1_1_cmp_o), .j(pcw), .Ai(jump16_2_1_ai));
  Multiplexer #(.Selector_Bits(2), .Bits(16)) multiplexer_2 (
    .sel(decode16a1_1_d_sel), .in_0(PC), .in_1(alu16_2_1_r), .in_2(test_A), .in_3(test_B),
    .out(multiplexer_2_out));
  Multiplexer #(.Bits(16)) multiplexer_3 (.sel(pcw), .in_0(multiplexer_2_out), .in_1(jump16_2_1_ai), .out(R));
  // Probe on A_2
  // Probe on A_2
  // Probe on A_2
  // Probe on R
  // Probe on R
  // Probe on R
endmodule

/* Test case:
C *PC     *A       A       R       rw pcw brk  test_A  test_B
0  0x0000  0x0000  X       X       0  0   0    0x0000  0x0000

# data word
C  0x0005  0x0000  X       X       0  0   0    0x0005  0x0000

# b = 1 + 1
C  0x8A02  0x0000  X       X       0  0   0    0x0005  0x0002

# a = a + 1
C  0x8201  0x0000  X       X       0  0   0    0x0006  0x0002
C  0x8201  0x0000  X       X       0  0   0    0x0007  0x0002
C  0x8201  0x0000  X       X       0  0   0    0x0008  0x0002
C  0x8201  0x0000  X       X       0  0   0    0x0009  0x0002
C  0x8201  0x0000  X       X       0  0   0    0x000A  0x0002
C  0x8201  0x0000  X       X       0  0   0    0x000B  0x0002
C  0x8201  0x0000  X       X       0  0   0    0x000C  0x0002
C  0x8201  0x0000  X       X       0  0   0    0x000D  0x0002
C  0x8201  0x0000  X       X       0  0   0    0x000E  0x0002
C  0x8201  0x0000  X       X       0  0   0    0x000F  0x0002

# a > 0 jmp b
C  0xA001  0x0000  X       X       0  1   0    0x000F  0x0002
*/
