// Digital circuit test1.dig as structural Verilog
module test1 (
  input  a,
  input  b,
  input  s,
  output x
);

  wire and_1_out, and_2_out;

  and and_1 (and_1_out, a, ~s);  // And
  and and_2 (and_2_out, b, s);
  or or_1 (x, and_1_out, and_2_out);
endmodule

/* Test case multiplexer test:
a b s x
0 0 0 0
0 1 0 0
1 0 0 1
1 1 0 1

0 0 1 0
0 1 1 1
1 0 1 0
1 1 1 1
*/
